// Logisim project ALU.circ as structural Verilog: 19 circuits, main circuit tester
module tester (
  input  in_1
);

  wire alu_1_cf, alu_1_q0, alu_1_q1, alu_1_q2, alu_1_q3, alu_1_q4, alu_1_q5, alu_1_q6, alu_1_q7, alu_1_so,
       alu_1_uo, alu_1_zf, buffer_1_out, button_1_out, clock_1_out, controlunitjmp_1_alu_reg_out,
       controlunitjmp_1_alui, controlunitjmp_1_aregister_in, controlunitjmp_1_aregister_out,
       controlunitjmp_1_bregister_in, controlunitjmp_1_counter_0, controlunitjmp_1_counter_1,
       controlunitjmp_1_counter_2, controlunitjmp_1_counter_enable, controlunitjmp_1_counter_out,
       controlunitjmp_1_dec, controlunitjmp_1_dec_in, controlunitjmp_1_fri, controlunitjmp_1_hlt,
       controlunitjmp_1_inc, controlunitjmp_1_instructionregister_in,
       controlunitjmp_1_instructionregister_out, controlunitjmp_1_jump, controlunitjmp_1_mar_in,
       controlunitjmp_1_outputregister_in, controlunitjmp_1_ram_in, controlunitjmp_1_ram_out,
       controlunitjmp_1_sub, decoder_1_out1, dipswitch_1_sw1, dipswitch_1_sw2, dipswitch_1_sw3,
       dipswitch_1_sw4, flags_register_4b02587d_1_out_8, flags_register_4b02587d_1_out_9,
       flags_register_4b02587d_1_out_10, flags_register_4b02587d_1_out_11, flags_register_4b02587d_1_q3,
       l_8_register_1c04c8bc_1_l0, l_8_register_1c04c8bc_1_l1, l_8_register_1c04c8bc_1_l2,
       l_8_register_1c04c8bc_1_l3, l_8_register_1c04c8bc_1_l4, l_8_register_1c04c8bc_1_l5,
       l_8_register_1c04c8bc_1_l6, l_8_register_1c04c8bc_1_l7, l_8_register_1c04c8bc_1_q0_led,
       l_8_register_1c04c8bc_1_q1_led, l_8_register_1c04c8bc_1_q2_led, l_8_register_1c04c8bc_1_q3_led,
       l_8_register_1c04c8bc_1_q4_led, l_8_register_1c04c8bc_1_q5_led, l_8_register_1c04c8bc_1_q6_led,
       l_8_register_1c04c8bc_1_q7_led, l_8_register_1c04c8bc_2_l0, l_8_register_1c04c8bc_2_l1,
       l_8_register_1c04c8bc_2_l2, l_8_register_1c04c8bc_2_l3, l_8_register_1c04c8bc_2_l4,
       l_8_register_1c04c8bc_2_l5, l_8_register_1c04c8bc_2_l6, l_8_register_1c04c8bc_2_l7,
       l_8_register_1c04c8bc_2_q0_led, l_8_register_1c04c8bc_2_q1_led, l_8_register_1c04c8bc_2_q2_led,
       l_8_register_1c04c8bc_2_q3_led, l_8_register_1c04c8bc_2_q4_led, l_8_register_1c04c8bc_2_q5_led,
       l_8_register_1c04c8bc_2_q6_led, l_8_register_1c04c8bc_2_q7_led, l_8_register_1c04c8bc_3_l0,
       l_8_register_1c04c8bc_3_l1, l_8_register_1c04c8bc_3_l2, l_8_register_1c04c8bc_3_l3,
       l_8_register_1c04c8bc_3_l4, l_8_register_1c04c8bc_3_l5, l_8_register_1c04c8bc_3_l6,
       l_8_register_1c04c8bc_3_l7, l_8_register_1c04c8bc_3_q4_led, l_8_register_1c04c8bc_3_q5_led,
       l_8_register_1c04c8bc_3_q6_led, l_8_register_1c04c8bc_3_q7_led, l_8_register_1c04c8bc_4_l0,
       l_8_register_1c04c8bc_4_l1, l_8_register_1c04c8bc_4_l2, l_8_register_1c04c8bc_4_l3,
       l_8_register_1c04c8bc_4_l4, l_8_register_1c04c8bc_4_l5, l_8_register_1c04c8bc_4_l6,
       l_8_register_1c04c8bc_4_l7, mar_4bit_1_l0, mar_4bit_1_l1, mar_4bit_1_l2, mar_4bit_1_l3, nor_1_out,
       not_1_out, not_2_out, not_3_out, program_counter_1_l0, program_counter_1_l1, program_counter_1_l2,
       program_counter_1_l3, program_counter_1_l4, program_counter_1_l5, program_counter_1_l6,
       program_counter_1_l7;
  wire [2:0] controlunitjmp_1_s2;
  wire [3:0] mar_4bit_1_y0;
  wire [6:0] rom_1_data, rom_2_data, rom_3_data, rom_4_data;
  wire [7:0] l_8_register_1c04c8bc_4_q0_led, program_counter_1_busout, ram_1_data;
  wire [8:8] l_1_bit_register_0a47a288_1_q0;

  DotMatrix #(.matrixcols(3), .matrixrows(1), .dotshape("circle")) dotmatrix_1 (
    .col0(controlunitjmp_1_counter_2), .col1(controlunitjmp_1_counter_1), .col2(controlunitjmp_1_counter_0));
  Clock clock_1 (.out(clock_1_out));
  ControlUnitJMP controlunitjmp_1 (
    .CLR(buffer_1_out), .Enable(1'b1), .I0(l_8_register_1c04c8bc_3_q4_led),
    .I1(l_8_register_1c04c8bc_3_q5_led), .I2(l_8_register_1c04c8bc_3_q6_led),
    .I3(l_8_register_1c04c8bc_3_q7_led), .CF(flags_register_4b02587d_1_q3), .S2(controlunitjmp_1_s2[0]),
    .S1(controlunitjmp_1_s2[1]), .S0(controlunitjmp_1_s2[2]), .DEC_IN(controlunitjmp_1_dec_in),
    .DEC(controlunitjmp_1_dec), .INC(controlunitjmp_1_inc), .SUB(controlunitjmp_1_sub),
    .Jump(controlunitjmp_1_jump), .Counter_OUT(controlunitjmp_1_counter_out),
    .Counter_Enable(controlunitjmp_1_counter_enable), .OutputRegister_IN(controlunitjmp_1_outputregister_in),
    .BRegister_IN(controlunitjmp_1_bregister_in), .ALU_REG_OUT(controlunitjmp_1_alu_reg_out),
    .ARegister_OUT(controlunitjmp_1_aregister_out), .ARegister_IN(controlunitjmp_1_aregister_in),
    .InstructionRegister_IN(controlunitjmp_1_instructionregister_in),
    .InstructionRegister_OUT(controlunitjmp_1_instructionregister_out), .RAM_OUT(controlunitjmp_1_ram_out),
    .RAM_IN(controlunitjmp_1_ram_in), .MAR_IN(controlunitjmp_1_mar_in), .HLT(controlunitjmp_1_hlt),
    .FRI(controlunitjmp_1_fri), .Counter_2(controlunitjmp_1_counter_2),
    .Counter_1(controlunitjmp_1_counter_1), .Counter_0(controlunitjmp_1_counter_0), .CLK(nor_1_out),
    .ALUI(controlunitjmp_1_alui));
  not not_1 (not_1_out, clock_1_out);
  nor nor_1 (nor_1_out, controlunitjmp_1_hlt, not_1_out);
  Button button_1 (.out(button_1_out));
  DipSwitch #(.number(4)) dipswitch_1 (
    .sw1(dipswitch_1_sw1), .sw2(dipswitch_1_sw2), .sw3(dipswitch_1_sw3), .sw4(dipswitch_1_sw4));
  buf buffer_1 (buffer_1_out, button_1_out);
  not not_2 (not_2_out, nor_1_out);
  LED led_1 (.in(program_counter_1_l7));
  LED led_2 (.in(program_counter_1_l6));
  LED led_3 (.in(program_counter_1_l4));
  LED led_4 (.in(program_counter_1_l5));
  LED led_5 (.in(program_counter_1_l3));
  MAR_4bit mar_4bit_1 (
    .CLK(nor_1_out), .A0(program_counter_1_busout[0]), .A1(program_counter_1_busout[1]),
    .A2(program_counter_1_busout[2]), .A3(program_counter_1_busout[3]), .Y0(mar_4bit_1_y0[0]),
    .Y1(mar_4bit_1_y0[1]), .Y2(mar_4bit_1_y0[2]), .Y3(mar_4bit_1_y0[3]), .Send(1'b1), .B3(dipswitch_1_sw4),
    .B2(dipswitch_1_sw3), .B1(dipswitch_1_sw2), .B0(dipswitch_1_sw1), .load(controlunitjmp_1_mar_in),
    .CLR(buffer_1_out), .L0(mar_4bit_1_l0), .L1(mar_4bit_1_l1), .L2(mar_4bit_1_l2), .L3(mar_4bit_1_l3));  // open: Select
  LED led_6 (.in(mar_4bit_1_l3));
  LED led_7 (.in(mar_4bit_1_l2));
  RAM #(.addrWidth(4), .trigger("falling")) ram_1 (
    .addr(mar_4bit_1_y0), .we(controlunitjmp_1_ram_in), .oe(controlunitjmp_1_ram_out), .clk(nor_1_out),
    .data(ram_1_data));
  DotMatrix #(.matrixcols(8), .matrixrows(1), .dotshape("circle")) dotmatrix_2 (
    .col0(l_8_register_1c04c8bc_1_l7), .col1(l_8_register_1c04c8bc_1_l6), .col2(l_8_register_1c04c8bc_1_l5),
    .col3(l_8_register_1c04c8bc_1_l4), .col4(l_8_register_1c04c8bc_1_l3), .col5(l_8_register_1c04c8bc_1_l2),
    .col6(l_8_register_1c04c8bc_1_l1), .col7(l_8_register_1c04c8bc_1_l0));
  DotMatrix #(.matrixcols(8), .matrixrows(1), .dotshape("circle")) dotmatrix_3 (
    .col0(l_8_register_1c04c8bc_2_l7), .col1(l_8_register_1c04c8bc_2_l6), .col2(l_8_register_1c04c8bc_2_l5),
    .col3(l_8_register_1c04c8bc_2_l4), .col4(l_8_register_1c04c8bc_2_l3), .col5(l_8_register_1c04c8bc_2_l2),
    .col6(l_8_register_1c04c8bc_2_l1), .col7(l_8_register_1c04c8bc_2_l0));
  DotMatrix #(.matrixcols(8), .matrixrows(1), .dotshape("circle")) dotmatrix_4 (
    .col0(l_8_register_1c04c8bc_3_l7), .col1(l_8_register_1c04c8bc_3_l6), .col2(l_8_register_1c04c8bc_3_l5),
    .col3(l_8_register_1c04c8bc_3_l4), .col4(l_8_register_1c04c8bc_3_l3), .col5(l_8_register_1c04c8bc_3_l2),
    .col6(l_8_register_1c04c8bc_3_l1), .col7(l_8_register_1c04c8bc_3_l0));
  LED led_8 (.in(program_counter_1_l2));
  LED led_9 (.in(program_counter_1_l0));
  LED led_10 (.in(program_counter_1_l1));
  Program_counter program_counter_1 (
    .CLR(buffer_1_out), .Load(controlunitjmp_1_jump), .Mode(controlunitjmp_1_counter_enable),
    .Enable(controlunitjmp_1_counter_enable), .CLK(nor_1_out), .BusIn(program_counter_1_busout),
    .BusOut(program_counter_1_busout), .L7(program_counter_1_l7), .L6(program_counter_1_l6),
    .L5(program_counter_1_l5), .L4(program_counter_1_l4), .L3(program_counter_1_l3),
    .L2(program_counter_1_l2), .L1(program_counter_1_l1), .L0(program_counter_1_l0),
    .send(controlunitjmp_1_counter_out));
  LED led_11 (.in(mar_4bit_1_l0));
  LED led_12 (.in(mar_4bit_1_l1));
  Pull_Resistor pull_resistor_1 (.node(program_counter_1_busout[5]));
  Pull_Resistor pull_resistor_2 (.node(program_counter_1_busout[4]));
  L_8_register_1c04c8bc l_8_register_1c04c8bc_1 (
    .Send(in_1), .Load(controlunitjmp_1_bregister_in), .D0(program_counter_1_busout[0]),
    .D1(program_counter_1_busout[1]), .D2(program_counter_1_busout[2]), .D3(program_counter_1_busout[3]),
    .D4(program_counter_1_busout[4]), .D5(program_counter_1_busout[5]), .D6(program_counter_1_busout[6]),
    .D7(program_counter_1_busout[7]), .Q0(program_counter_1_busout[0]), .Q1(program_counter_1_busout[1]),
    .Q2(program_counter_1_busout[2]), .Q3(program_counter_1_busout[3]), .Q4(program_counter_1_busout[4]),
    .Q5(program_counter_1_busout[5]), .Q6(program_counter_1_busout[6]), .Q7(program_counter_1_busout[7]),
    .Q7_LED(l_8_register_1c04c8bc_1_q7_led), .Q6_LED(l_8_register_1c04c8bc_1_q6_led),
    .Q5_LED(l_8_register_1c04c8bc_1_q5_led), .Q4_LED(l_8_register_1c04c8bc_1_q4_led),
    .Q3_LED(l_8_register_1c04c8bc_1_q3_led), .Q2_LED(l_8_register_1c04c8bc_1_q2_led),
    .Q1_LED(l_8_register_1c04c8bc_1_q1_led), .Q0_LED(l_8_register_1c04c8bc_1_q0_led),
    .L0(l_8_register_1c04c8bc_1_l0), .L1(l_8_register_1c04c8bc_1_l1), .L2(l_8_register_1c04c8bc_1_l2),
    .L3(l_8_register_1c04c8bc_1_l3), .L4(l_8_register_1c04c8bc_1_l4), .L5(l_8_register_1c04c8bc_1_l5),
    .L6(l_8_register_1c04c8bc_1_l6), .L7(l_8_register_1c04c8bc_1_l7), .CLK(nor_1_out), .CLR(buffer_1_out));
  L_8_register_1c04c8bc l_8_register_1c04c8bc_2 (
    .Send(controlunitjmp_1_aregister_out), .Load(controlunitjmp_1_aregister_in),
    .D0(program_counter_1_busout[0]), .D1(program_counter_1_busout[1]), .D2(program_counter_1_busout[2]),
    .D3(program_counter_1_busout[3]), .D4(program_counter_1_busout[4]), .D5(program_counter_1_busout[5]),
    .D6(program_counter_1_busout[6]), .D7(program_counter_1_busout[7]), .Q0(program_counter_1_busout[0]),
    .Q1(program_counter_1_busout[1]), .Q2(program_counter_1_busout[2]), .Q3(program_counter_1_busout[3]),
    .Q4(program_counter_1_busout[4]), .Q5(program_counter_1_busout[5]), .Q6(program_counter_1_busout[6]),
    .Q7(program_counter_1_busout[7]), .Q7_LED(l_8_register_1c04c8bc_2_q7_led),
    .Q6_LED(l_8_register_1c04c8bc_2_q6_led), .Q5_LED(l_8_register_1c04c8bc_2_q5_led),
    .Q4_LED(l_8_register_1c04c8bc_2_q4_led), .Q3_LED(l_8_register_1c04c8bc_2_q3_led),
    .Q2_LED(l_8_register_1c04c8bc_2_q2_led), .Q1_LED(l_8_register_1c04c8bc_2_q1_led),
    .Q0_LED(l_8_register_1c04c8bc_2_q0_led), .L0(l_8_register_1c04c8bc_2_l0),
    .L1(l_8_register_1c04c8bc_2_l1), .L2(l_8_register_1c04c8bc_2_l2), .L3(l_8_register_1c04c8bc_2_l3),
    .L4(l_8_register_1c04c8bc_2_l4), .L5(l_8_register_1c04c8bc_2_l5), .L6(l_8_register_1c04c8bc_2_l6),
    .L7(l_8_register_1c04c8bc_2_l7), .CLK(not_2_out), .CLR(buffer_1_out));
  L_8_register_1c04c8bc l_8_register_1c04c8bc_3 (
    .Send(controlunitjmp_1_instructionregister_out), .Load(controlunitjmp_1_instructionregister_in),
    .D0(program_counter_1_busout[0]), .D1(program_counter_1_busout[1]), .D2(program_counter_1_busout[2]),
    .D3(program_counter_1_busout[3]), .D4(program_counter_1_busout[4]), .D5(program_counter_1_busout[5]),
    .D6(program_counter_1_busout[6]), .D7(program_counter_1_busout[7]), .Q0(program_counter_1_busout[0]),
    .Q1(program_counter_1_busout[1]), .Q2(program_counter_1_busout[2]), .Q3(program_counter_1_busout[3]),
    .Q7_LED(l_8_register_1c04c8bc_3_q7_led), .Q6_LED(l_8_register_1c04c8bc_3_q6_led),
    .Q5_LED(l_8_register_1c04c8bc_3_q5_led), .Q4_LED(l_8_register_1c04c8bc_3_q4_led),
    .L0(l_8_register_1c04c8bc_3_l0), .L1(l_8_register_1c04c8bc_3_l1), .L2(l_8_register_1c04c8bc_3_l2),
    .L3(l_8_register_1c04c8bc_3_l3), .L4(l_8_register_1c04c8bc_3_l4), .L5(l_8_register_1c04c8bc_3_l5),
    .L6(l_8_register_1c04c8bc_3_l6), .L7(l_8_register_1c04c8bc_3_l7), .CLK(nor_1_out), .CLR(buffer_1_out));  // open: Q4, Q5, Q6, Q7, Q3_LED, Q2_LED, Q1_LED, Q0_LED
  LED led_13 (.in(program_counter_1_busout[7]));
  Pull_Resistor pull_resistor_3 (.node(program_counter_1_busout[7]));
  Pull_Resistor pull_resistor_4 (.node(program_counter_1_busout[6]));
  LED led_14 (.in(program_counter_1_busout[6]));
  LED led_15 (.in(program_counter_1_busout[5]));
  LED led_16 (.in(program_counter_1_busout[4]));
  LED led_17 (.in(program_counter_1_busout[3]));
  LED led_18 (.in(program_counter_1_busout[0]));
  LED led_19 (.in(program_counter_1_busout[2]));
  LED led_20 (.in(program_counter_1_busout[1]));
  Pull_Resistor pull_resistor_5 (.node(program_counter_1_busout[0]));
  Pull_Resistor pull_resistor_6 (.node(program_counter_1_busout[1]));
  Pull_Resistor pull_resistor_7 (.node(program_counter_1_busout[2]));
  Pull_Resistor pull_resistor_8 (.node(program_counter_1_busout[3]));
  DotMatrix #(.matrixcols(8), .matrixrows(1), .dotshape("circle")) dotmatrix_5 (
    .col0(l_8_register_1c04c8bc_4_l7), .col1(l_8_register_1c04c8bc_4_l6), .col2(l_8_register_1c04c8bc_4_l5),
    .col3(l_8_register_1c04c8bc_4_l4), .col4(l_8_register_1c04c8bc_4_l3), .col5(l_8_register_1c04c8bc_4_l2),
    .col6(l_8_register_1c04c8bc_4_l1), .col7(l_8_register_1c04c8bc_4_l0));
  ALU alu_1 (
    .A0(l_8_register_1c04c8bc_2_q0_led), .B0(l_8_register_1c04c8bc_1_q0_led),
    .Subtract(controlunitjmp_1_sub), .Inc(controlunitjmp_1_inc), .A1(l_8_register_1c04c8bc_2_q1_led),
    .Dec_in(controlunitjmp_1_dec_in), .B1(l_8_register_1c04c8bc_1_q1_led), .Dec(controlunitjmp_1_dec),
    .Select(controlunitjmp_1_s2), .A2(l_8_register_1c04c8bc_2_q2_led), .B2(l_8_register_1c04c8bc_1_q2_led),
    .A3(l_8_register_1c04c8bc_2_q3_led), .B3(l_8_register_1c04c8bc_1_q3_led),
    .A4(l_8_register_1c04c8bc_2_q4_led), .B4(l_8_register_1c04c8bc_1_q4_led),
    .A5(l_8_register_1c04c8bc_2_q5_led), .B5(l_8_register_1c04c8bc_1_q5_led),
    .A6(l_8_register_1c04c8bc_2_q6_led), .B6(l_8_register_1c04c8bc_1_q6_led),
    .A7(l_8_register_1c04c8bc_2_q7_led), .B7(l_8_register_1c04c8bc_1_q7_led), .Uo(alu_1_uo), .Q7(alu_1_q7),
    .Q6(alu_1_q6), .Q5(alu_1_q5), .Q4(alu_1_q4), .Q3(alu_1_q3), .Q2(alu_1_q2), .Q1(alu_1_q1), .Q0(alu_1_q0),
    .So(alu_1_so), .ZF(alu_1_zf), .CF(alu_1_cf), .Send(1'b1));
  RAM_BUS ram_bus_1 (
    .in_2(program_counter_1_busout[0]), .in_3(program_counter_1_busout[1]),
    .in_4(program_counter_1_busout[2]), .in_5(program_counter_1_busout[3]),
    .in_6(program_counter_1_busout[4]), .in_7(program_counter_1_busout[5]),
    .in_8(program_counter_1_busout[6]), .L1(program_counter_1_busout[7]), .send(controlunitjmp_1_ram_out),
    .out_27(ram_1_data[0]), .out_28(ram_1_data[1]), .out_29(ram_1_data[2]), .out_30(ram_1_data[3]),
    .out_31(ram_1_data[4]), .out_32(ram_1_data[5]), .out_33(ram_1_data[6]), .out_34(ram_1_data[7]),
    .out_19(program_counter_1_busout[7]), .out_20(program_counter_1_busout[6]),
    .out_21(program_counter_1_busout[5]), .out_22(program_counter_1_busout[4]),
    .out_23(program_counter_1_busout[3]), .out_24(program_counter_1_busout[2]),
    .out_25(program_counter_1_busout[1]), .out_26(program_counter_1_busout[0]), .in_10(ram_1_data[7]),
    .in_11(ram_1_data[6]), .in_12(ram_1_data[5]), .in_13(ram_1_data[4]), .in_14(ram_1_data[3]),
    .in_15(ram_1_data[2]), .in_16(ram_1_data[1]), .S0(ram_1_data[0]), .load(controlunitjmp_1_ram_in));
  not not_3 (not_3_out, nor_1_out);
  L_8_register_1c04c8bc l_8_register_1c04c8bc_4 (
    .Load(controlunitjmp_1_outputregister_in), .D0(program_counter_1_busout[0]),
    .D1(program_counter_1_busout[1]), .D2(program_counter_1_busout[2]), .D3(program_counter_1_busout[3]),
    .D4(program_counter_1_busout[4]), .D5(program_counter_1_busout[5]), .D6(program_counter_1_busout[6]),
    .D7(program_counter_1_busout[7]), .Q0(program_counter_1_busout[0]), .Q1(program_counter_1_busout[1]),
    .Q2(program_counter_1_busout[2]), .Q3(program_counter_1_busout[3]), .Q4(program_counter_1_busout[4]),
    .Q5(program_counter_1_busout[5]), .Q6(program_counter_1_busout[6]), .Q7(program_counter_1_busout[7]),
    .Q7_LED(l_8_register_1c04c8bc_4_q0_led[7]), .Q6_LED(l_8_register_1c04c8bc_4_q0_led[6]),
    .Q5_LED(l_8_register_1c04c8bc_4_q0_led[5]), .Q4_LED(l_8_register_1c04c8bc_4_q0_led[4]),
    .Q3_LED(l_8_register_1c04c8bc_4_q0_led[3]), .Q2_LED(l_8_register_1c04c8bc_4_q0_led[2]),
    .Q1_LED(l_8_register_1c04c8bc_4_q0_led[1]), .Q0_LED(l_8_register_1c04c8bc_4_q0_led[0]),
    .L0(l_8_register_1c04c8bc_4_l0), .L1(l_8_register_1c04c8bc_4_l1), .L2(l_8_register_1c04c8bc_4_l2),
    .L3(l_8_register_1c04c8bc_4_l3), .L4(l_8_register_1c04c8bc_4_l4), .L5(l_8_register_1c04c8bc_4_l5),
    .L6(l_8_register_1c04c8bc_4_l6), .L7(l_8_register_1c04c8bc_4_l7), .CLK(nor_1_out), .CLR(buffer_1_out));  // open: Send
  Decoder #(.select(3), .enable("false")) decoder_1 (
    .out1(decoder_1_out1), .sel(controlunitjmp_1_s2));  // open: out0, out2, out3, out4, out5, out6, out7
  L_1_bit_register_0a47a288 l_1_bit_register_0a47a288_1 (
    .Send(1'b1), .Load(decoder_1_out1), .D0(decoder_1_out1), .CLK(not_3_out),
    .Q0(l_1_bit_register_0a47a288_1_q0[8]));
  LED led_21 (.in(flags_register_4b02587d_1_out_8));
  LED led_22 (.in(flags_register_4b02587d_1_out_11));
  LED led_23 (.in(flags_register_4b02587d_1_out_9));
  LED led_24 (.in(flags_register_4b02587d_1_out_10));
  Flags_Register_4b02587d flags_register_4b02587d_1 (
    .Send(1'b1), .Load(controlunitjmp_1_fri), .D0(alu_1_uo), .CLK(nor_1_out), .D1(alu_1_so), .D2(alu_1_zf),
    .D3(alu_1_cf), .Q3(flags_register_4b02587d_1_q3), .out_8(flags_register_4b02587d_1_out_8),
    .out_9(flags_register_4b02587d_1_out_9), .out_10(flags_register_4b02587d_1_out_10),
    .out_11(flags_register_4b02587d_1_out_11));  // open: Q0, Q1, Q2
  ROM #(.addrWidth(9), .dataWidth(7)) rom_1 (
    .addr({l_1_bit_register_0a47a288_1_q0[8], l_8_register_1c04c8bc_4_q0_led}), .data(rom_1_data));
  ROM #(.addrWidth(9), .dataWidth(7)) rom_2 (
    .addr({l_1_bit_register_0a47a288_1_q0[8], l_8_register_1c04c8bc_4_q0_led}), .data(rom_2_data));
  ROM #(.addrWidth(9), .dataWidth(7)) rom_3 (
    .addr({l_1_bit_register_0a47a288_1_q0[8], l_8_register_1c04c8bc_4_q0_led}), .data(rom_3_data));
  ROM #(.addrWidth(9), .dataWidth(7)) rom_4 (
    .addr({l_1_bit_register_0a47a288_1_q0[8], l_8_register_1c04c8bc_4_q0_led}), .data(rom_4_data));
  L_8_register_1c04c8bc l_8_register_1c04c8bc_5 (
    .Send(controlunitjmp_1_alu_reg_out), .Load(controlunitjmp_1_alui), .D0(alu_1_q0), .D1(alu_1_q1),
    .D2(alu_1_q2), .D3(alu_1_q3), .D4(alu_1_q4), .D5(alu_1_q5), .D6(alu_1_q6), .D7(alu_1_q7),
    .Q0(program_counter_1_busout[0]), .Q1(program_counter_1_busout[1]), .Q2(program_counter_1_busout[2]),
    .Q3(program_counter_1_busout[3]), .Q4(program_counter_1_busout[4]), .Q5(program_counter_1_busout[5]),
    .Q6(program_counter_1_busout[6]), .Q7(program_counter_1_busout[7]), .CLK(nor_1_out));  // open: Q7_LED, Q6_LED, Q5_LED, Q4_LED, Q3_LED, Q2_LED, Q1_LED, Q0_LED, L0, L1, L2, L3, L4, L5, L6, L7, CLR
  _7_Segment_Display #(.active("false")) u_7_segment_display_1 (
    .g(rom_4_data[0]), .f(rom_4_data[1]), .a(rom_4_data[6]), .b(rom_4_data[5]), .e(rom_4_data[2]),
    .d(rom_4_data[3]), .c(rom_4_data[4]), .dp(1'b1));
  _7_Segment_Display #(.active("false")) u_7_segment_display_2 (
    .g(rom_2_data[0]), .f(rom_2_data[1]), .a(rom_2_data[6]), .b(rom_2_data[5]), .e(rom_2_data[2]),
    .d(rom_2_data[3]), .c(rom_2_data[4]), .dp(1'b1));
  _7_Segment_Display #(.active("false")) u_7_segment_display_3 (
    .g(rom_3_data[0]), .f(rom_3_data[1]), .a(rom_3_data[6]), .b(rom_3_data[5]), .e(rom_3_data[2]),
    .d(rom_3_data[3]), .c(rom_3_data[4]), .dp(1'b1));
  _7_Segment_Display #(.active("false")) u_7_segment_display_4 (
    .g(rom_1_data[0]), .f(rom_1_data[1]), .a(rom_1_data[6]), .b(rom_1_data[5]), .e(rom_1_data[2]),
    .d(rom_1_data[3]), .c(rom_1_data[4]), .dp(1'b1));

  // Notes on the sheet:
  //   B Register
  //   A Register
  //   contents of rom_1 (hex, n*v repeats v):
  //   1 4f 12 6 4c 24 20 f 0 4 1 4f 12 6 4c 24 20 f 0 4 1 4f 12 6 4c 24 20 f 0 4 1 4f 12 6 4c 24 20 f 0 4
  //   1 4f 12 6 4c 24 20 f 0 4 1 4f 12 6 4c 24 20 f 0 4 1 4f 12 6 4c 24 20 f 0 4 1 4f 12 6 4c 24 20 f 0 4
  //   1 4f 12 6 4c 24 20 f 0 4 1 4f 12 6 4c 24 20 f 0 4 1 4f 12 6 4c 24 20 f 0 4 1 4f 12 6 4c 24 20 f 0 4
  //   1 4f 12 6 4c 24 20 f 0 4 1 4f 12 6 4c 24 20 f 0 4 1 4f 12 6 4c 24 20 f 0 4 1 4f 12 6 4c 24 20 f 0 4
  //   1 4f 12 6 4c 24 20 f 0 4 1 4f 12 6 4c 24 20 f 0 4 1 4f 12 6 4c 24 20 f 0 4 1 4f 12 6 4c 24 20 f 0 4
  //   1 4f 12 6 4c 24 20 f 0 4 1 4f 12 6 4c 24 20 f 0 4 1 4f 12 6 4c 24 20 f 0 4 1 4f 12 6 4c 24 20 f 0 4
  //   1 4f 12 6 4c 24 20 f 0 4 1 4f 12 6 4c 24 1 4f 12 6 4c 24 20 f 0 4 1 4f 12 6 4c 24 20 f 0 4 1 4f 12 6
  //   4c 24 20 f 0 4 1 4f 12 6 4c 24 20 f 0 4 1 4f 12 6 4c 24 20 f 0 4 1 4f 12 6 4c 24 20 f 0 4 1 4f 12 6
  //   4c 24 20 f 0 4 1 4f 12 6 4c 24 20 f 0 4 1 4f 12 6 4c 24 20 f 0 4 1 4f 12 6 4c 24 20 f 0 4 1 4f 12 6
  //   4c 24 20 f 0 4 1 4f 12 6 4c 24 20 f 0 4 1 4f 12 6 4c 24 20 f 0 f 20 24 4c 6 12 4f 1 4 0 f 20 24 4c 6
  //   12 4f 1 4 0 f 20 24 4c 6 12 4f 1 4 0 f 20 24 4c 6 12 4f 1 4 0 f 20 24 4c 6 12 4f 1 4 0 f 20 24 4c 6
  //   12 4f 1 4 0 f 20 24 4c 6 12 4f 1 4 0 f 20 24 4c 6 12 4f 1 4 0 f 20 24 4c 6 12 4f 1 4 0 f 20 24 4c 6
  //   12 4f 1 4 0 f 20 24 4c 6 12 4f 1 4 0 f 20 24 4c 6 12 4f 1 4 0 f 20 24 4c 6 12 4f
  //   contents of rom_2 (hex, n*v repeats v):
  //   7f 9*1 10*4f 10*12 10*6 10*4c 10*24 10*20 10*f 10*0 10*4 10*1 10*4f 10*12 10*6 10*4c 10*24 10*20
  //   10*f 10*0 10*4 10*1 10*4f 10*12 10*6 10*4c 6*24 10*1 10*4f 10*12 10*6 10*4c 10*24 10*20 10*f 10*0
  //   10*4 10*1 10*4f 17*12 10*4f 10*1 10*4 10*0 10*f 10*20 10*24 10*4c 10*6 10*12 10*4f 9*1
  //   contents of rom_3 (hex, n*v repeats v):
  //   7f 99*1 100*4f 56*12 100*1 57*4f 99*1
  //   contents of rom_4 (hex, n*v repeats v):
  //   384*7f 128*7e
endmodule

module L_8_bit_ALU_slice_e4fc08b7 (
  input  A,
  input  B,
  input  Comp,
  input  Cin,
  input  [2:0] S,
  input  inc,
  input  Dec,
  input  Dec_in,
  output Q,
  output Cout,
  output Inc_out,
  output Dec_out
);

  wire and_2_out, and_3_out, and_4_out, and_5_out, and_6_out, not_1_out, or_1_out, xor_1_out, xor_2_out,
       xor_3_out, xor_4_out, xor_5_out, xor_6_out, xor_7_out;

  xor xor_1 (xor_1_out, B, Comp);
  xor xor_2 (xor_2_out, inc, A);
  xor xor_3 (xor_3_out, A, Dec);
  xor xor_4 (xor_4_out, A, xor_1_out);
  and and_1 (Inc_out, inc, A);
  and and_2 (and_2_out, A, Dec);
  and and_3 (and_3_out, xor_3_out, Dec_in);
  and and_4 (and_4_out, xor_1_out, A);
  and and_5 (and_5_out, xor_4_out, Cin);
  or or_1 (or_1_out, A, B);
  not not_1 (not_1_out, A);
  and and_6 (and_6_out, A, B);
  xor xor_5 (xor_5_out, A, B);
  xor xor_6 (xor_6_out, xor_4_out, Cin);
  xor xor_7 (xor_7_out, xor_3_out, Dec_in);
  or or_2 (Dec_out, and_2_out, and_3_out);
  or or_3 (Cout, and_4_out, and_5_out);
  Multiplexer #(.select(3), .enable("false")) multiplexer_1 (
    .in0(xor_6_out), .in1(xor_6_out), .in2(or_1_out), .in3(not_1_out), .in4(xor_2_out), .in5(xor_7_out),
    .in6(xor_5_out), .in7(and_6_out), .out(Q), .sel(S));

  // Notes on the sheet:
  //   A OR B
  //   NOT A
  //   A AND B
  //   A XOR B
  //   INCREMENT A
  //   DECREMENT A
  //   A + B / A - B
endmodule

module ALU (
  input  A0,
  input  B0,
  input  Subtract,
  input  Inc,
  input  A1,
  input  Dec_in,
  input  B1,
  input  Dec,
  input  [2:0] Select,
  input  A2,
  input  B2,
  input  A3,
  input  B3,
  input  A4,
  input  B4,
  input  A5,
  input  B5,
  input  Send,
  input  A6,
  input  B6,
  input  A7,
  input  B7,
  output So,
  output CF,
  output Q7,
  output Q6,
  output Q5,
  output Q4,
  output Q3,
  output Q2,
  output Q1,
  output Q0,
  output Uo,
  output ZF
);

  wire l_8_bit_alu_slice_e4fc08b7_1_cout, l_8_bit_alu_slice_e4fc08b7_1_dec_out,
       l_8_bit_alu_slice_e4fc08b7_1_inc_out, l_8_bit_alu_slice_e4fc08b7_1_q,
       l_8_bit_alu_slice_e4fc08b7_2_cout, l_8_bit_alu_slice_e4fc08b7_2_dec_out,
       l_8_bit_alu_slice_e4fc08b7_2_inc_out, l_8_bit_alu_slice_e4fc08b7_2_q,
       l_8_bit_alu_slice_e4fc08b7_3_cout, l_8_bit_alu_slice_e4fc08b7_3_dec_out,
       l_8_bit_alu_slice_e4fc08b7_3_inc_out, l_8_bit_alu_slice_e4fc08b7_3_q,
       l_8_bit_alu_slice_e4fc08b7_4_cout, l_8_bit_alu_slice_e4fc08b7_4_dec_out,
       l_8_bit_alu_slice_e4fc08b7_4_inc_out, l_8_bit_alu_slice_e4fc08b7_4_q,
       l_8_bit_alu_slice_e4fc08b7_5_cout, l_8_bit_alu_slice_e4fc08b7_5_dec_out,
       l_8_bit_alu_slice_e4fc08b7_5_inc_out, l_8_bit_alu_slice_e4fc08b7_5_q,
       l_8_bit_alu_slice_e4fc08b7_6_cout, l_8_bit_alu_slice_e4fc08b7_6_dec_out,
       l_8_bit_alu_slice_e4fc08b7_6_inc_out, l_8_bit_alu_slice_e4fc08b7_6_q,
       l_8_bit_alu_slice_e4fc08b7_7_cout, l_8_bit_alu_slice_e4fc08b7_7_dec_out,
       l_8_bit_alu_slice_e4fc08b7_7_inc_out, l_8_bit_alu_slice_e4fc08b7_7_q,
       l_8_bit_alu_slice_e4fc08b7_8_cout, l_8_bit_alu_slice_e4fc08b7_8_inc_out,
       l_8_bit_alu_slice_e4fc08b7_8_q, or_2_out;

  L_8_bit_ALU_slice_e4fc08b7 l_8_bit_alu_slice_e4fc08b7_1 (
    .A(A0), .B(B0), .Comp(Subtract), .Cin(Subtract), .S(Select), .inc(Inc), .Dec_in(Dec_in),
    .Inc_out(l_8_bit_alu_slice_e4fc08b7_1_inc_out), .Dec_out(l_8_bit_alu_slice_e4fc08b7_1_dec_out),
    .Cout(l_8_bit_alu_slice_e4fc08b7_1_cout), .Q(l_8_bit_alu_slice_e4fc08b7_1_q), .Dec(Dec));
  L_8_bit_ALU_slice_e4fc08b7 l_8_bit_alu_slice_e4fc08b7_2 (
    .A(A1), .B(B1), .Comp(Subtract), .Cin(l_8_bit_alu_slice_e4fc08b7_1_cout), .S(Select),
    .inc(l_8_bit_alu_slice_e4fc08b7_1_inc_out), .Dec_in(l_8_bit_alu_slice_e4fc08b7_1_dec_out),
    .Inc_out(l_8_bit_alu_slice_e4fc08b7_2_inc_out), .Dec_out(l_8_bit_alu_slice_e4fc08b7_2_dec_out),
    .Cout(l_8_bit_alu_slice_e4fc08b7_2_cout), .Q(l_8_bit_alu_slice_e4fc08b7_2_q), .Dec(Dec));
  L_8_bit_ALU_slice_e4fc08b7 l_8_bit_alu_slice_e4fc08b7_3 (
    .A(A2), .B(B2), .Comp(Subtract), .Cin(l_8_bit_alu_slice_e4fc08b7_2_cout), .S(Select),
    .inc(l_8_bit_alu_slice_e4fc08b7_2_inc_out), .Dec_in(l_8_bit_alu_slice_e4fc08b7_2_dec_out),
    .Inc_out(l_8_bit_alu_slice_e4fc08b7_3_inc_out), .Dec_out(l_8_bit_alu_slice_e4fc08b7_3_dec_out),
    .Cout(l_8_bit_alu_slice_e4fc08b7_3_cout), .Q(l_8_bit_alu_slice_e4fc08b7_3_q), .Dec(Dec));
  L_8_bit_ALU_slice_e4fc08b7 l_8_bit_alu_slice_e4fc08b7_4 (
    .A(A3), .B(B3), .Comp(Subtract), .Cin(l_8_bit_alu_slice_e4fc08b7_3_cout), .S(Select),
    .inc(l_8_bit_alu_slice_e4fc08b7_3_inc_out), .Dec_in(l_8_bit_alu_slice_e4fc08b7_3_dec_out),
    .Inc_out(l_8_bit_alu_slice_e4fc08b7_4_inc_out), .Dec_out(l_8_bit_alu_slice_e4fc08b7_4_dec_out),
    .Cout(l_8_bit_alu_slice_e4fc08b7_4_cout), .Q(l_8_bit_alu_slice_e4fc08b7_4_q), .Dec(Dec));
  L_8_bit_ALU_slice_e4fc08b7 l_8_bit_alu_slice_e4fc08b7_5 (
    .A(A4), .B(B4), .Comp(Subtract), .Cin(l_8_bit_alu_slice_e4fc08b7_4_cout), .S(Select),
    .inc(l_8_bit_alu_slice_e4fc08b7_4_inc_out), .Dec_in(l_8_bit_alu_slice_e4fc08b7_4_dec_out),
    .Inc_out(l_8_bit_alu_slice_e4fc08b7_5_inc_out), .Dec_out(l_8_bit_alu_slice_e4fc08b7_5_dec_out),
    .Cout(l_8_bit_alu_slice_e4fc08b7_5_cout), .Q(l_8_bit_alu_slice_e4fc08b7_5_q), .Dec(Dec));
  L_8_bit_ALU_slice_e4fc08b7 l_8_bit_alu_slice_e4fc08b7_6 (
    .A(A5), .B(B5), .Comp(Subtract), .Cin(l_8_bit_alu_slice_e4fc08b7_5_cout), .S(Select),
    .inc(l_8_bit_alu_slice_e4fc08b7_5_inc_out), .Dec_in(l_8_bit_alu_slice_e4fc08b7_5_dec_out),
    .Inc_out(l_8_bit_alu_slice_e4fc08b7_6_inc_out), .Dec_out(l_8_bit_alu_slice_e4fc08b7_6_dec_out),
    .Cout(l_8_bit_alu_slice_e4fc08b7_6_cout), .Q(l_8_bit_alu_slice_e4fc08b7_6_q), .Dec(Dec));
  L_8_bit_ALU_slice_e4fc08b7 l_8_bit_alu_slice_e4fc08b7_7 (
    .A(A6), .B(B6), .Comp(Subtract), .Cin(l_8_bit_alu_slice_e4fc08b7_6_cout), .S(Select),
    .inc(l_8_bit_alu_slice_e4fc08b7_6_inc_out), .Dec_in(l_8_bit_alu_slice_e4fc08b7_6_dec_out),
    .Inc_out(l_8_bit_alu_slice_e4fc08b7_7_inc_out), .Dec_out(l_8_bit_alu_slice_e4fc08b7_7_dec_out),
    .Cout(l_8_bit_alu_slice_e4fc08b7_7_cout), .Q(l_8_bit_alu_slice_e4fc08b7_7_q), .Dec(Dec));
  L_8_bit_ALU_slice_e4fc08b7 l_8_bit_alu_slice_e4fc08b7_8 (
    .A(A7), .B(B7), .Comp(Subtract), .Cin(l_8_bit_alu_slice_e4fc08b7_7_cout), .S(Select),
    .inc(l_8_bit_alu_slice_e4fc08b7_7_inc_out), .Dec_in(l_8_bit_alu_slice_e4fc08b7_7_dec_out),
    .Inc_out(l_8_bit_alu_slice_e4fc08b7_8_inc_out), .Cout(l_8_bit_alu_slice_e4fc08b7_8_cout),
    .Q(l_8_bit_alu_slice_e4fc08b7_8_q), .Dec(Dec));  // open: Dec_out
  xor xor_1 (So, l_8_bit_alu_slice_e4fc08b7_7_cout, l_8_bit_alu_slice_e4fc08b7_8_cout);
  or or_1 (CF, l_8_bit_alu_slice_e4fc08b7_8_cout, l_8_bit_alu_slice_e4fc08b7_8_inc_out);
  xor xor_2 (Uo, l_8_bit_alu_slice_e4fc08b7_8_cout, Subtract);
  assign Q5 = or_2_out ? l_8_bit_alu_slice_e4fc08b7_6_q : 1'bz;  // Controlled_Buffer controlled_buffer_1
  assign Q7 = or_2_out ? l_8_bit_alu_slice_e4fc08b7_8_q : 1'bz;  // Controlled_Buffer controlled_buffer_2
  assign Q4 = or_2_out ? l_8_bit_alu_slice_e4fc08b7_5_q : 1'bz;  // Controlled_Buffer controlled_buffer_3
  assign Q6 = or_2_out ? l_8_bit_alu_slice_e4fc08b7_7_q : 1'bz;  // Controlled_Buffer controlled_buffer_4
  assign Q0 = or_2_out ? l_8_bit_alu_slice_e4fc08b7_1_q : 1'bz;  // Controlled_Buffer controlled_buffer_5
  assign Q2 = or_2_out ? l_8_bit_alu_slice_e4fc08b7_3_q : 1'bz;  // Controlled_Buffer controlled_buffer_6
  assign Q1 = or_2_out ? l_8_bit_alu_slice_e4fc08b7_2_q : 1'bz;  // Controlled_Buffer controlled_buffer_7
  assign Q3 = or_2_out ? l_8_bit_alu_slice_e4fc08b7_4_q : 1'bz;  // Controlled_Buffer controlled_buffer_8
  nor nor_1 (ZF, Q7, Q6, Q5, Q4, Q3, Q2, Q1, Q0);
  or or_2 (or_2_out, Send, 1'b1);
endmodule

module test (
  input  [2:0] in_1,
  input  [7:0] in_2,
  input  in_3,
  input  in_4,
  input  in_5,
  input  in_6,
  input  in_7,
  input  in_8,
  input  in_9,
  input  in_10,
  input  in_11,
  input  in_12,
  input  in_13,
  input  in_14,
  input  in_15,
  input  in_16,
  input  in_17,
  input  in_18,
  input  in_19,
  input  in_20,
  input  in_21,
  input  in_22,
  input  [7:0] in_23,
  input  in_24,
  input  in_25,
  input  in_26,
  input  in_27,
  input  in_28,
  input  in_29,
  input  in_30,
  input  [7:0] in_31,
  input  in_32,
  input  in_33,
  input  in_34,
  input  in_35,
  input  [7:0] in_36,
  input  [15:0] in_37,
  output out_38,
  output out_39,
  output [11:0] out_40
);

  wire and_1_out, and_2_out, clock_1_out, clock_2_out, clock_3_out, clock_4_out, clock_5_out,
       controlunit_1_aregister_in, controlunit_1_counter_out, controlunit_1_instructionregister_in,
       controlunit_1_instructionregister_out, controlunit_1_mar_in, controlunit_1_ram_out, decoder_1_out1,
       dipswitch_1_sw1, dipswitch_1_sw2, dipswitch_1_sw3, dipswitch_1_sw4, hex_decoder_1_a, hex_decoder_1_b,
       hex_decoder_1_c, hex_decoder_1_d, hex_decoder_1_e, hex_decoder_1_f, hex_decoder_1_g,
       l_8_register_1c04c8bc_1_q4, l_8_register_1c04c8bc_1_q4_led, l_8_register_1c04c8bc_1_q5,
       l_8_register_1c04c8bc_1_q5_led, l_8_register_1c04c8bc_1_q6, l_8_register_1c04c8bc_1_q6_led,
       l_8_register_1c04c8bc_1_q7, l_8_register_1c04c8bc_1_q7_led, mar_4bit_2_y0, not_1_out, not_2_out,
       not_3_out, or_1_out, program_counter_1_p3, pull_resistor_1_node, pull_resistor_2_node, xor_1_out,
       xor_2_out, xor_3_out, xor_4_out;
  wire [3:0] mar_4bit_1_y0;
  wire [6:0] rom_1_data, rom_2_data, rom_3_data, rom_4_data, rom_5_data;
  wire [7:0] ram_1_data;
  wire [15:0] ram_2_data;

  Clock clock_1 (.out(clock_1_out));
  Clock clock_2 (.out(clock_2_out));
  Decoder #(.select(3), .enable("false")) decoder_1 (
    .out1(decoder_1_out1), .sel(in_1));  // open: out0, out2, out3, out4, out5, out6, out7
  L_1_bit_register_0a47a288 l_1_bit_register_0a47a288_1 (
    .Send(decoder_1_out1), .Load(1'b1), .D0(decoder_1_out1), .CLK(clock_1_out), .Q0(out_38));
  ROM #(.addrWidth(9), .dataWidth(7)) rom_1 (.addr({in_22, in_23}), .data(rom_1_data));
  ROM #(.addrWidth(9), .dataWidth(7)) rom_2 (.addr({in_22, in_23}), .data(rom_2_data));
  ROM #(.addrWidth(9), .dataWidth(7)) rom_3 (.addr({in_22, in_23}), .data(rom_3_data));
  ROM #(.addrWidth(9), .dataWidth(7)) rom_4 (.addr({in_22, in_23}), .data(rom_4_data));
  DipSwitch #(.number(4)) dipswitch_1 (
    .sw1(dipswitch_1_sw1), .sw2(dipswitch_1_sw2), .sw3(dipswitch_1_sw3), .sw4(dipswitch_1_sw4));
  MAR_4bit mar_4bit_1 (
    .CLK(clock_2_out), .A0(l_8_register_1c04c8bc_1_q7), .A1(l_8_register_1c04c8bc_1_q6),
    .A2(l_8_register_1c04c8bc_1_q5), .A3(l_8_register_1c04c8bc_1_q4), .Select(in_20), .Y0(mar_4bit_1_y0[0]),
    .Y1(mar_4bit_1_y0[1]), .Y2(mar_4bit_1_y0[2]), .Y3(mar_4bit_1_y0[3]), .Send(in_19), .B3(dipswitch_1_sw4),
    .B2(dipswitch_1_sw3), .B1(dipswitch_1_sw2), .B0(dipswitch_1_sw1), .load(controlunit_1_mar_in));  // open: CLR, L0, L1, L2, L3
  Bit_Extender #(.in_width(16), .out_width(12), .\type ("zero")) bit_extender_1 (.in(in_37), .out(out_40));
  RAM #(.addrWidth(4), .trigger("falling")) ram_1 (
    .addr(mar_4bit_1_y0), .we(in_21), .oe(controlunit_1_ram_out), .clk(clock_2_out), .data(ram_1_data));
  ROM #(.dataWidth(7)) rom_5 (.addr(in_2), .data(rom_5_data));
  _7_Segment_Display #(.active("false")) u_7_segment_display_1 (
    .g(rom_4_data[0]), .f(rom_4_data[1]), .a(rom_4_data[6]), .b(rom_4_data[5]), .e(rom_4_data[2]),
    .d(rom_4_data[3]), .c(rom_4_data[4]), .dp(pull_resistor_1_node));
  RAM #(.addrWidth(12), .dataWidth(16)) ram_2 (.addr(out_40), .data(ram_2_data));  // open: we, oe, clk
  Mar_8bit mar_8bit_1 (
    .CLK(clock_2_out), .load(in_10), .A0(in_18), .A1(in_16), .A2(in_17), .A3(in_15), .A4(in_14), .A5(in_13),
    .A6(in_12), .A7(in_11), .Y0(ram_1_data[0]), .Y1(ram_1_data[1]), .Y2(ram_1_data[2]), .Y3(ram_1_data[3]),
    .Y4(ram_1_data[4]), .Y5(ram_1_data[5]), .Y6(ram_1_data[6]), .Y7(ram_1_data[7]), .Send(in_9), .CLR(in_8));  // open: B7, B6, B5, B4, B3, B2, B1, B0, B7_2, B6_2, B5_2, B4_2, B3_2, B2_2, B1_2, Bus0, Send_Bus
  _7_Segment_Display #(.active("false")) u_7_segment_display_2 (
    .g(rom_2_data[0]), .f(rom_2_data[1]), .a(rom_2_data[6]), .b(rom_2_data[5]), .e(rom_2_data[2]),
    .d(rom_2_data[3]), .c(rom_2_data[4]), .dp(pull_resistor_1_node));
  _7_Segment_Display #(.active("false")) u_7_segment_display_3 (
    .g(rom_3_data[0]), .f(rom_3_data[1]), .a(rom_3_data[6]), .b(rom_3_data[5]), .e(rom_3_data[2]),
    .d(rom_3_data[3]), .c(rom_3_data[4]), .dp(pull_resistor_1_node));
  _7_Segment_Display #(.active("false")) u_7_segment_display_4 (
    .g(rom_1_data[0]), .f(rom_1_data[1]), .a(rom_1_data[6]), .b(rom_1_data[5]), .e(rom_1_data[2]),
    .d(rom_1_data[3]), .c(rom_1_data[4]), .dp(pull_resistor_1_node));
  Clock clock_3 (.out(clock_3_out));
  Pull_Resistor #(.pull(1)) pull_resistor_1 (.node(pull_resistor_1_node));
  _7_Segment_Display #(.active("false")) u_7_segment_display_5 (
    .g(rom_5_data[0]), .f(rom_5_data[1]), .a(rom_5_data[6]), .b(rom_5_data[5]), .e(rom_5_data[2]),
    .d(rom_5_data[3]), .c(rom_5_data[4]), .dp(pull_resistor_2_node));
  Pull_Resistor #(.pull(1)) pull_resistor_2 (.node(pull_resistor_2_node));
  MAR_4bit mar_4bit_2 (
    .CLK(clock_3_out), .A3(in_28), .Y0(mar_4bit_2_y0), .Send(in_30), .load(in_30));  // open: A0, A1, A2, Select, Y1, Y2, Y3, B3, B2, B1, B0, CLR, L0, L1, L2, L3
  ControlUnit controlunit_1 (
    .Enable(1'b1), .I0(l_8_register_1c04c8bc_1_q4_led), .I1(l_8_register_1c04c8bc_1_q5_led),
    .I2(l_8_register_1c04c8bc_1_q6_led), .I3(l_8_register_1c04c8bc_1_q7_led),
    .Counter_OUT(controlunit_1_counter_out), .ARegister_IN(controlunit_1_aregister_in),
    .InstructionRegister_IN(controlunit_1_instructionregister_in),
    .InstructionRegister_OUT(controlunit_1_instructionregister_out), .RAM_OUT(controlunit_1_ram_out),
    .MAR_IN(controlunit_1_mar_in), .CLK(clock_2_out));  // open: CLR, S2, S1, S0, DEC_IN, DEC, INC, SUB, Jump, Counter_Enable, OutputRegister_IN, BRegister_IN, ALU_REG_OUT, ARegister_OUT, RAM_IN, HLT, Counter_2, Counter_1, Counter_0
  Clock clock_4 (.out(clock_4_out));
  Clock clock_5 (.out(clock_5_out));
  not not_1 (not_1_out, clock_4_out);
  xor xor_1 (xor_1_out, in_26, in_27);
  not not_2 (not_2_out, clock_5_out);
  not not_3 (not_3_out, in_32);
  or or_1 (or_1_out, in_33, not_2_out);
  nor nor_1 (out_39, not_1_out, in_24);
  xor xor_2 (xor_2_out, in_25, xor_1_out);
  xor xor_3 (xor_3_out, not_3_out, or_1_out);
  MAR_4bit mar_4bit_3 (.CLK(clock_2_out));  // open: A0, A1, A2, A3, Select, Y0, Y1, Y2, Y3, Send, B3, B2, B1, B0, load, CLR, L0, L1, L2, L3
  and and_1 (and_1_out, xor_1_out, in_25);
  and and_2 (and_2_out, xor_2_out, in_29);
  L_8_register_1c04c8bc l_8_register_1c04c8bc_1 (
    .Send(controlunit_1_instructionregister_out), .Load(controlunit_1_instructionregister_in),
    .Q4(l_8_register_1c04c8bc_1_q4), .Q5(l_8_register_1c04c8bc_1_q5), .Q6(l_8_register_1c04c8bc_1_q6),
    .Q7(l_8_register_1c04c8bc_1_q7), .Q7_LED(l_8_register_1c04c8bc_1_q7_led),
    .Q6_LED(l_8_register_1c04c8bc_1_q6_led), .Q5_LED(l_8_register_1c04c8bc_1_q5_led),
    .Q4_LED(l_8_register_1c04c8bc_1_q4_led), .CLK(clock_2_out));  // open: D0, D1, D2, D3, D4, D5, D6, D7, Q0, Q1, Q2, Q3, Q3_LED, Q2_LED, Q1_LED, Q0_LED, L0, L1, L2, L3, L4, L5, L6, L7, CLR
  // Program_counter program_counter_1: pin names not known; wires that end beside it: clock_2_out, controlunit_1_counter_out, program_counter_1_p3, program_counter_1_p3
  L_8_register_1c04c8bc l_8_register_1c04c8bc_2 (
    .Load(controlunit_1_aregister_in), .CLK(clock_2_out));  // open: Send, D0, D1, D2, D3, D4, D5, D6, D7, Q0, Q1, Q2, Q3, Q4, Q5, Q6, Q7, Q7_LED, Q6_LED, Q5_LED, Q4_LED, Q3_LED, Q2_LED, Q1_LED, Q0_LED, L0, L1, L2, L3, L4, L5, L6, L7, CLR
  xor xor_4 (xor_4_out, xor_2_out, in_29);
  // OR_Gate or_2 has open pins: in0=and_1_out, in1=and_2_out, out=open
  RAM #(.trigger("falling")) ram_3 (.addr(in_31), .we(in_35), .oe(in_34), .clk(xor_3_out), .data(in_36));
  Hex_Decoder hex_decoder_1 (
    .D3(in_4), .D2(in_5), .D1(in_6), .D0(in_7), .A(hex_decoder_1_a), .B(hex_decoder_1_b),
    .C(hex_decoder_1_c), .D(hex_decoder_1_d), .E(hex_decoder_1_e), .F(hex_decoder_1_f), .G(hex_decoder_1_g));
  _7_Segment_Display #(.active("false")) u_7_segment_display_6 (
    .g(hex_decoder_1_g), .f(hex_decoder_1_f), .a(hex_decoder_1_a), .b(hex_decoder_1_b), .e(hex_decoder_1_e),
    .d(hex_decoder_1_d), .c(hex_decoder_1_c), .dp(in_3));

  // Notes on the sheet:
  //   contents of rom_1 (hex, n*v repeats v):
  //   1 4f 12 6 4c 24 20 f 0 4 1 4f 12 6 4c 24 20 f 0 4 1 4f 12 6 4c 24 20 f 0 4 1 4f 12 6 4c 24 20 f 0 4
  //   1 4f 12 6 4c 24 20 f 0 4 1 4f 12 6 4c 24 20 f 0 4 1 4f 12 6 4c 24 20 f 0 4 1 4f 12 6 4c 24 20 f 0 4
  //   1 4f 12 6 4c 24 20 f 0 4 1 4f 12 6 4c 24 20 f 0 4 1 4f 12 6 4c 24 20 f 0 4 1 4f 12 6 4c 24 20 f 0 4
  //   1 4f 12 6 4c 24 20 f 0 4 1 4f 12 6 4c 24 20 f 0 4 1 4f 12 6 4c 24 20 f 0 4 1 4f 12 6 4c 24 20 f 0 4
  //   1 4f 12 6 4c 24 20 f 0 4 1 4f 12 6 4c 24 20 f 0 4 1 4f 12 6 4c 24 20 f 0 4 1 4f 12 6 4c 24 20 f 0 4
  //   1 4f 12 6 4c 24 20 f 0 4 1 4f 12 6 4c 24 20 f 0 4 1 4f 12 6 4c 24 20 f 0 4 1 4f 12 6 4c 24 20 f 0 4
  //   1 4f 12 6 4c 24 20 f 0 4 1 4f 12 6 4c 24 1 4f 12 6 4c 24 20 f 0 4 1 4f 12 6 4c 24 20 f 0 4 1 4f 12 6
  //   4c 24 20 f 0 4 1 4f 12 6 4c 24 20 f 0 4 1 4f 12 6 4c 24 20 f 0 4 1 4f 12 6 4c 24 20 f 0 4 1 4f 12 6
  //   4c 24 20 f 0 4 1 4f 12 6 4c 24 20 f 0 4 1 4f 12 6 4c 24 20 f 0 4 1 4f 12 6 4c 24 20 f 0 4 1 4f 12 6
  //   4c 24 20 f 0 4 1 4f 12 6 4c 24 20 f 0 4 1 4f 12 6 4c 24 20 f 0 f 20 24 4c 6 12 4f 1 4 0 f 20 24 4c 6
  //   12 4f 1 4 0 f 20 24 4c 6 12 4f 1 4 0 f 20 24 4c 6 12 4f 1 4 0 f 20 24 4c 6 12 4f 1 4 0 f 20 24 4c 6
  //   12 4f 1 4 0 f 20 24 4c 6 12 4f 1 4 0 f 20 24 4c 6 12 4f 1 4 0 f 20 24 4c 6 12 4f 1 4 0 f 20 24 4c 6
  //   12 4f 1 4 0 f 20 24 4c 6 12 4f 1 4 0 f 20 24 4c 6 12 4f 1 4 0 f 20 24 4c 6 12 4f
  //   contents of rom_2 (hex, n*v repeats v):
  //   10*1 10*4f 10*12 10*6 10*4c 10*24 10*20 10*f 10*0 10*4 4f 8*1 9*4f 10*12 10*6 10*4c 10*24 10*20 10*f
  //   10*0 10*4 4f 4f 4f 8*1 7*4f 10*12 10*6 10*4c 10*24 10*1 10*4f 10*12 10*6 10*4c 10*24 10*20 10*f 10*0
  //   10*4 10*1 10*4f 17*12 10*4f 10*1 10*4 10*0 10*f 10*20 10*24 10*4c 10*6 10*12 10*4f 9*1
  //   contents of rom_3 (hex, n*v repeats v):
  //   100*1 108*4f 48*12 100*1 57*4f 99*1
  //   contents of rom_4 (hex, n*v repeats v):
  //   384*7f 128*7e
  //   contents of rom_5 (hex, n*v repeats v):
  //   1 4f 12 6 4c 24 20 f 0 4 8 60 31 42 30 38
endmodule

module D_flip_flop_560ac045 (
  input  CLK,
  input  D,
  output Q,
  output Qinv
);

  wire and_1_out, and_2_out, not_1_out;

  not not_1 (not_1_out, D);
  and and_1 (and_1_out, not_1_out, CLK);
  and and_2 (and_2_out, CLK, D);
  nor nor_1 (Q, and_1_out, Qinv);
  nor nor_2 (Qinv, Q, and_2_out);
endmodule

module L_8_register_1c04c8bc (
  input  Send,
  input  Load,
  input  D0,
  input  CLK,
  input  D1,
  input  D2,
  input  D3,
  input  D4,
  input  D5,
  input  D6,
  input  D7,
  input  CLR,
  output Q7_LED,
  output Q6_LED,
  output Q5_LED,
  output Q4_LED,
  output Q3_LED,
  output Q2_LED,
  output Q1_LED,
  output Q0_LED,
  output L7,
  output L6,
  output L5,
  output L4,
  output L3,
  output L2,
  output L1,
  output L0,
  output Q0,
  output Q1,
  output Q2,
  output Q3,
  output Q4,
  output Q5,
  output Q6,
  output Q7
);

  wire and_1_out, and_2_out, and_3_out, and_4_out, and_5_out, and_6_out, and_7_out, and_8_out, and_9_out,
       and_10_out, and_11_out, and_12_out, and_13_out, and_14_out, and_15_out, and_16_out, not_1_out,
       not_2_out, not_3_out, not_4_out, not_5_out, not_6_out, not_7_out, not_8_out, or_1_out, or_2_out,
       or_3_out, or_4_out, or_5_out, or_6_out, or_7_out, or_8_out;

  not not_1 (not_1_out, Load);
  not not_2 (not_2_out, Load);
  not not_3 (not_3_out, Load);
  not not_4 (not_4_out, Load);
  not not_5 (not_5_out, Load);
  not not_6 (not_6_out, Load);
  not not_7 (not_7_out, Load);
  not not_8 (not_8_out, Load);
  and and_1 (and_1_out, L0, not_1_out);
  and and_2 (and_2_out, Load, D0);
  and and_3 (and_3_out, L1, not_2_out);
  and and_4 (and_4_out, Load, D1);
  and and_5 (and_5_out, L2, not_3_out);
  and and_6 (and_6_out, Load, D2);
  and and_7 (and_7_out, L3, not_4_out);
  and and_8 (and_8_out, Load, D3);
  and and_9 (and_9_out, L4, not_5_out);
  and and_10 (and_10_out, Load, D4);
  and and_11 (and_11_out, L5, not_6_out);
  and and_12 (and_12_out, Load, D5);
  and and_13 (and_13_out, L6, not_7_out);
  and and_14 (and_14_out, Load, D6);
  and and_15 (and_15_out, L7, not_8_out);
  and and_16 (and_16_out, Load, D7);
  or or_1 (or_1_out, and_1_out, and_2_out);
  or or_2 (or_2_out, and_3_out, and_4_out);
  or or_3 (or_3_out, and_5_out, and_6_out);
  or or_4 (or_4_out, and_7_out, and_8_out);
  or or_5 (or_5_out, and_9_out, and_10_out);
  or or_6 (or_6_out, and_11_out, and_12_out);
  or or_7 (or_7_out, and_13_out, and_14_out);
  or or_8 (or_8_out, and_15_out, and_16_out);
  D_Flip_Flop d_ff_1 (.D(or_1_out), .clk(CLK), .Q(L0), .reset(CLR));  // open: Qn, preset
  D_Flip_Flop d_ff_2 (.D(or_2_out), .clk(CLK), .Q(L1), .reset(CLR));  // open: Qn, preset
  D_Flip_Flop d_ff_3 (.D(or_3_out), .clk(CLK), .Q(L2), .reset(CLR));  // open: Qn, preset
  D_Flip_Flop d_ff_4 (.D(or_4_out), .clk(CLK), .Q(L3), .reset(CLR));  // open: Qn, preset
  D_Flip_Flop d_ff_5 (.D(or_5_out), .clk(CLK), .Q(L4), .reset(CLR));  // open: Qn, preset
  D_Flip_Flop d_ff_6 (.D(or_6_out), .clk(CLK), .Q(L5), .reset(CLR));  // open: Qn, preset
  D_Flip_Flop d_ff_7 (.D(or_7_out), .clk(CLK), .Q(L6), .reset(CLR));  // open: Qn, preset
  D_Flip_Flop d_ff_8 (.D(or_8_out), .clk(CLK), .Q(L7), .reset(CLR));  // open: Qn, preset
  assign Q0 = Send ? L0 : 1'bz;  // Controlled_Buffer controlled_buffer_1
  assign Q1 = Send ? L1 : 1'bz;  // Controlled_Buffer controlled_buffer_2
  assign Q2 = Send ? L2 : 1'bz;  // Controlled_Buffer controlled_buffer_3
  assign Q3 = Send ? L3 : 1'bz;  // Controlled_Buffer controlled_buffer_4
  assign Q4 = Send ? L4 : 1'bz;  // Controlled_Buffer controlled_buffer_5
  assign Q5 = Send ? L5 : 1'bz;  // Controlled_Buffer controlled_buffer_6
  assign Q6 = Send ? L6 : 1'bz;  // Controlled_Buffer controlled_buffer_7
  assign Q7 = Send ? L7 : 1'bz;  // Controlled_Buffer controlled_buffer_8

  assign Q0_LED = L0;
  assign Q1_LED = L1;
  assign Q2_LED = L2;
  assign Q3_LED = L3;
  assign Q4_LED = L4;
  assign Q5_LED = L5;
  assign Q6_LED = L6;
  assign Q7_LED = L7;
endmodule

module Flags_Register_4b02587d (
  input  Send,
  input  Load,
  input  D0,
  input  CLK,
  input  D1,
  input  D2,
  input  D3,
  output out_8,
  output out_9,
  output out_10,
  output out_11,
  output Q0,
  output Q1,
  output Q2,
  output Q3
);

  wire and_1_out, and_2_out, and_3_out, and_4_out, and_5_out, and_6_out, and_7_out, and_8_out, not_1_out,
       not_2_out, not_3_out, not_4_out, or_1_out, or_2_out, or_3_out, or_4_out;

  not not_1 (not_1_out, Load);
  not not_2 (not_2_out, Load);
  not not_3 (not_3_out, Load);
  not not_4 (not_4_out, Load);
  and and_1 (and_1_out, out_11, not_1_out);
  and and_2 (and_2_out, Load, D0);
  and and_3 (and_3_out, out_10, not_2_out);
  and and_4 (and_4_out, Load, D1);
  and and_5 (and_5_out, out_9, not_3_out);
  and and_6 (and_6_out, Load, D2);
  and and_7 (and_7_out, out_8, not_4_out);
  and and_8 (and_8_out, Load, D3);
  or or_1 (or_1_out, and_1_out, and_2_out);
  or or_2 (or_2_out, and_3_out, and_4_out);
  or or_3 (or_3_out, and_5_out, and_6_out);
  or or_4 (or_4_out, and_7_out, and_8_out);
  D_Flip_Flop d_ff_1 (.D(or_1_out), .clk(CLK), .Q(out_11));  // open: Qn, preset, reset
  D_Flip_Flop d_ff_2 (.D(or_2_out), .clk(CLK), .Q(out_10));  // open: Qn, preset, reset
  D_Flip_Flop d_ff_3 (.D(or_3_out), .clk(CLK), .Q(out_9));  // open: Qn, preset, reset
  D_Flip_Flop d_ff_4 (.D(or_4_out), .clk(CLK), .Q(out_8));  // open: Qn, preset, reset
  assign Q0 = Send ? out_11 : 1'bz;  // Controlled_Buffer controlled_buffer_1
  assign Q1 = Send ? out_10 : 1'bz;  // Controlled_Buffer controlled_buffer_2
  assign Q2 = Send ? out_9 : 1'bz;  // Controlled_Buffer controlled_buffer_3
  assign Q3 = Send ? out_8 : 1'bz;  // Controlled_Buffer controlled_buffer_4
endmodule

module L_1_bit_register_0a47a288 (
  input  Send,
  input  Load,
  input  D0,
  input  CLK,
  output Q0
);

  wire and_1_out, and_2_out, d_ff_1_q, not_1_out, or_1_out;

  not not_1 (not_1_out, Load);
  and and_1 (and_1_out, d_ff_1_q, not_1_out);
  and and_2 (and_2_out, Load, D0);
  D_Flip_Flop d_ff_1 (.D(or_1_out), .clk(CLK), .Q(d_ff_1_q));  // open: Qn, preset, reset
  or or_1 (or_1_out, and_1_out, and_2_out);
  assign Q0 = Send ? d_ff_1_q : 1'bz;  // Controlled_Buffer controlled_buffer_1
endmodule

module L_32_Byte_RAM_5bbffe80 (
  input  CLK,
  input  in_2,
  input  in_3,
  input  in_4,
  input  in_5,
  input  in_6,
  input  in_7,
  input  in_8,
  input  in_9,
  input  in_10,
  input  in_11,
  input  in_12,
  input  in_13,
  input  in_14,
  input  in_15,
  input  in_16,
  input  in_17,
  input  in_18,
  input  in_19,
  input  in_20,
  input  in_21,
  input  in_22,
  input  in_23,
  input  in_24,
  input  in_25,
  input  in_26,
  input  in_27,
  input  in_28,
  input  in_29,
  input  in_30,
  input  in_31,
  input  in_32,
  input  in_33,
  input  in_34,
  input  in_35,
  input  in_36,
  input  in_37,
  input  in_38,
  input  in_39,
  input  in_40,
  input  in_41,
  input  in_42,
  input  in_43,
  input  in_44,
  input  in_45,
  input  in_46,
  input  in_47,
  input  in_48,
  input  in_49,
  input  in_50,
  input  in_51,
  input  in_52,
  input  in_53,
  input  in_54,
  input  in_55,
  input  in_56,
  input  in_57,
  input  in_58,
  input  in_59,
  input  in_60,
  input  in_61,
  input  in_62,
  input  in_63,
  input  in_64,
  input  in_65,
  output out_66,
  output out_67,
  output out_68,
  output out_69,
  output out_70,
  output out_71,
  output out_72,
  output out_73
);

  wire l_1_bit_register_0a47a288_229_q0, l_1_bit_register_0a47a288_237_q0, l_1_bit_register_0a47a288_245_q0,
       l_1_bit_register_0a47a288_253_q0;

  L_1_bit_register_0a47a288 l_1_bit_register_0a47a288_1 (.Send(in_2), .Load(in_3), .D0(out_66), .CLK(CLK), .Q0(out_66));
  L_1_bit_register_0a47a288 l_1_bit_register_0a47a288_2 (.Send(in_4), .Load(in_5), .D0(out_66), .CLK(CLK), .Q0(out_66));
  L_1_bit_register_0a47a288 l_1_bit_register_0a47a288_3 (.Send(in_6), .Load(in_7), .D0(out_66), .CLK(CLK), .Q0(out_66));
  L_1_bit_register_0a47a288 l_1_bit_register_0a47a288_4 (.Send(in_8), .Load(in_9), .D0(out_66), .CLK(CLK), .Q0(out_66));
  L_1_bit_register_0a47a288 l_1_bit_register_0a47a288_5 (
    .Send(in_10), .Load(in_11), .D0(out_66), .CLK(CLK), .Q0(out_66));
  L_1_bit_register_0a47a288 l_1_bit_register_0a47a288_6 (
    .Send(in_12), .Load(in_13), .D0(out_66), .CLK(CLK), .Q0(out_66));
  L_1_bit_register_0a47a288 l_1_bit_register_0a47a288_7 (
    .Send(in_14), .Load(in_15), .D0(out_66), .CLK(CLK), .Q0(out_66));
  L_1_bit_register_0a47a288 l_1_bit_register_0a47a288_8 (
    .Send(in_16), .Load(in_17), .D0(out_66), .CLK(CLK), .Q0(out_66));
  L_1_bit_register_0a47a288 l_1_bit_register_0a47a288_9 (
    .Send(in_18), .Load(in_19), .D0(out_66), .CLK(CLK), .Q0(out_66));
  L_1_bit_register_0a47a288 l_1_bit_register_0a47a288_10 (
    .Send(in_20), .Load(in_21), .D0(out_66), .CLK(CLK), .Q0(out_66));
  L_1_bit_register_0a47a288 l_1_bit_register_0a47a288_11 (
    .Send(in_22), .Load(in_23), .D0(out_66), .CLK(CLK), .Q0(out_66));
  L_1_bit_register_0a47a288 l_1_bit_register_0a47a288_12 (
    .Send(in_24), .Load(in_25), .D0(out_66), .CLK(CLK), .Q0(out_66));
  L_1_bit_register_0a47a288 l_1_bit_register_0a47a288_13 (
    .Send(in_26), .Load(in_27), .D0(out_66), .CLK(CLK), .Q0(out_66));
  L_1_bit_register_0a47a288 l_1_bit_register_0a47a288_14 (
    .Send(in_28), .Load(in_29), .D0(out_66), .CLK(CLK), .Q0(out_66));
  L_1_bit_register_0a47a288 l_1_bit_register_0a47a288_15 (
    .Send(in_30), .Load(in_31), .D0(out_66), .CLK(CLK), .Q0(out_66));
  L_1_bit_register_0a47a288 l_1_bit_register_0a47a288_16 (
    .Send(in_32), .Load(in_33), .D0(out_66), .CLK(CLK), .Q0(out_66));
  L_1_bit_register_0a47a288 l_1_bit_register_0a47a288_17 (
    .Send(in_34), .Load(in_35), .D0(out_66), .CLK(CLK), .Q0(out_66));
  L_1_bit_register_0a47a288 l_1_bit_register_0a47a288_18 (
    .Send(in_36), .Load(in_37), .D0(out_66), .CLK(CLK), .Q0(out_66));
  L_1_bit_register_0a47a288 l_1_bit_register_0a47a288_19 (
    .Send(in_38), .Load(in_39), .D0(out_66), .CLK(CLK), .Q0(out_66));
  L_1_bit_register_0a47a288 l_1_bit_register_0a47a288_20 (
    .Send(in_40), .Load(in_41), .D0(out_66), .CLK(CLK), .Q0(out_66));
  L_1_bit_register_0a47a288 l_1_bit_register_0a47a288_21 (
    .Send(in_42), .Load(in_43), .D0(out_66), .CLK(CLK), .Q0(out_66));
  L_1_bit_register_0a47a288 l_1_bit_register_0a47a288_22 (
    .Send(in_44), .Load(in_45), .D0(out_66), .CLK(CLK), .Q0(out_66));
  L_1_bit_register_0a47a288 l_1_bit_register_0a47a288_23 (
    .Send(in_46), .Load(in_47), .D0(out_66), .CLK(CLK), .Q0(out_66));
  L_1_bit_register_0a47a288 l_1_bit_register_0a47a288_24 (
    .Send(in_48), .Load(in_49), .D0(out_66), .CLK(CLK), .Q0(out_66));
  L_1_bit_register_0a47a288 l_1_bit_register_0a47a288_25 (
    .Send(in_50), .Load(in_51), .D0(out_66), .CLK(CLK), .Q0(out_66));
  L_1_bit_register_0a47a288 l_1_bit_register_0a47a288_26 (
    .Send(in_52), .Load(in_53), .D0(out_66), .CLK(CLK), .Q0(out_66));
  L_1_bit_register_0a47a288 l_1_bit_register_0a47a288_27 (
    .Send(in_54), .Load(in_55), .D0(out_66), .CLK(CLK), .Q0(out_66));
  L_1_bit_register_0a47a288 l_1_bit_register_0a47a288_28 (
    .Send(in_56), .Load(in_57), .D0(out_66), .CLK(CLK), .Q0(out_66));
  L_1_bit_register_0a47a288 l_1_bit_register_0a47a288_29 (
    .Send(in_58), .Load(in_59), .D0(out_66), .CLK(CLK), .Q0(out_66));
  L_1_bit_register_0a47a288 l_1_bit_register_0a47a288_30 (
    .Send(in_60), .Load(in_61), .D0(out_66), .CLK(CLK), .Q0(out_66));
  L_1_bit_register_0a47a288 l_1_bit_register_0a47a288_31 (
    .Send(in_62), .Load(in_63), .D0(out_66), .CLK(CLK), .Q0(out_66));
  L_1_bit_register_0a47a288 l_1_bit_register_0a47a288_32 (
    .Send(in_64), .Load(in_65), .D0(out_66), .CLK(CLK), .Q0(out_66));
  L_1_bit_register_0a47a288 l_1_bit_register_0a47a288_33 (
    .Send(in_2), .Load(in_3), .D0(out_67), .CLK(CLK), .Q0(out_67));
  L_1_bit_register_0a47a288 l_1_bit_register_0a47a288_34 (
    .Send(in_4), .Load(in_5), .D0(out_67), .CLK(CLK), .Q0(out_67));
  L_1_bit_register_0a47a288 l_1_bit_register_0a47a288_35 (
    .Send(in_6), .Load(in_7), .D0(out_67), .CLK(CLK), .Q0(out_67));
  L_1_bit_register_0a47a288 l_1_bit_register_0a47a288_36 (
    .Send(in_8), .Load(in_9), .D0(out_67), .CLK(CLK), .Q0(out_67));
  L_1_bit_register_0a47a288 l_1_bit_register_0a47a288_37 (
    .Send(in_10), .Load(in_11), .D0(out_67), .CLK(CLK), .Q0(out_67));
  L_1_bit_register_0a47a288 l_1_bit_register_0a47a288_38 (
    .Send(in_12), .Load(in_13), .D0(out_67), .CLK(CLK), .Q0(out_67));
  L_1_bit_register_0a47a288 l_1_bit_register_0a47a288_39 (
    .Send(in_14), .Load(in_15), .D0(out_67), .CLK(CLK), .Q0(out_67));
  L_1_bit_register_0a47a288 l_1_bit_register_0a47a288_40 (
    .Send(in_16), .Load(in_17), .D0(out_67), .CLK(CLK), .Q0(out_67));
  L_1_bit_register_0a47a288 l_1_bit_register_0a47a288_41 (
    .Send(in_18), .Load(in_19), .D0(out_67), .CLK(CLK), .Q0(out_67));
  L_1_bit_register_0a47a288 l_1_bit_register_0a47a288_42 (
    .Send(in_20), .Load(in_21), .D0(out_67), .CLK(CLK), .Q0(out_67));
  L_1_bit_register_0a47a288 l_1_bit_register_0a47a288_43 (
    .Send(in_22), .Load(in_23), .D0(out_67), .CLK(CLK), .Q0(out_67));
  L_1_bit_register_0a47a288 l_1_bit_register_0a47a288_44 (
    .Send(in_24), .Load(in_25), .D0(out_67), .CLK(CLK), .Q0(out_67));
  L_1_bit_register_0a47a288 l_1_bit_register_0a47a288_45 (
    .Send(in_26), .Load(in_27), .D0(out_67), .CLK(CLK), .Q0(out_67));
  L_1_bit_register_0a47a288 l_1_bit_register_0a47a288_46 (
    .Send(in_28), .Load(in_29), .D0(out_67), .CLK(CLK), .Q0(out_67));
  L_1_bit_register_0a47a288 l_1_bit_register_0a47a288_47 (
    .Send(in_30), .Load(in_31), .D0(out_67), .CLK(CLK), .Q0(out_67));
  L_1_bit_register_0a47a288 l_1_bit_register_0a47a288_48 (
    .Send(in_32), .Load(in_33), .D0(out_67), .CLK(CLK), .Q0(out_67));
  L_1_bit_register_0a47a288 l_1_bit_register_0a47a288_49 (
    .Send(in_34), .Load(in_35), .D0(out_67), .CLK(CLK), .Q0(out_67));
  L_1_bit_register_0a47a288 l_1_bit_register_0a47a288_50 (
    .Send(in_36), .Load(in_37), .D0(out_67), .CLK(CLK), .Q0(out_67));
  L_1_bit_register_0a47a288 l_1_bit_register_0a47a288_51 (
    .Send(in_38), .Load(in_39), .D0(out_67), .CLK(CLK), .Q0(out_67));
  L_1_bit_register_0a47a288 l_1_bit_register_0a47a288_52 (
    .Send(in_40), .Load(in_41), .D0(out_67), .CLK(CLK), .Q0(out_67));
  L_1_bit_register_0a47a288 l_1_bit_register_0a47a288_53 (
    .Send(in_42), .Load(in_43), .D0(out_67), .CLK(CLK), .Q0(out_67));
  L_1_bit_register_0a47a288 l_1_bit_register_0a47a288_54 (
    .Send(in_44), .Load(in_45), .D0(out_67), .CLK(CLK), .Q0(out_67));
  L_1_bit_register_0a47a288 l_1_bit_register_0a47a288_55 (
    .Send(in_46), .Load(in_47), .D0(out_67), .CLK(CLK), .Q0(out_67));
  L_1_bit_register_0a47a288 l_1_bit_register_0a47a288_56 (
    .Send(in_48), .Load(in_49), .D0(out_67), .CLK(CLK), .Q0(out_67));
  L_1_bit_register_0a47a288 l_1_bit_register_0a47a288_57 (
    .Send(in_50), .Load(in_51), .D0(out_67), .CLK(CLK), .Q0(out_67));
  L_1_bit_register_0a47a288 l_1_bit_register_0a47a288_58 (
    .Send(in_52), .Load(in_53), .D0(out_67), .CLK(CLK), .Q0(out_67));
  L_1_bit_register_0a47a288 l_1_bit_register_0a47a288_59 (
    .Send(in_54), .Load(in_55), .D0(out_67), .CLK(CLK), .Q0(out_67));
  L_1_bit_register_0a47a288 l_1_bit_register_0a47a288_60 (
    .Send(in_56), .Load(in_57), .D0(out_67), .CLK(CLK), .Q0(out_67));
  L_1_bit_register_0a47a288 l_1_bit_register_0a47a288_61 (
    .Send(in_58), .Load(in_59), .D0(out_67), .CLK(CLK), .Q0(out_67));
  L_1_bit_register_0a47a288 l_1_bit_register_0a47a288_62 (
    .Send(in_60), .Load(in_61), .D0(out_67), .CLK(CLK), .Q0(out_67));
  L_1_bit_register_0a47a288 l_1_bit_register_0a47a288_63 (
    .Send(in_62), .Load(in_63), .D0(out_67), .CLK(CLK), .Q0(out_67));
  L_1_bit_register_0a47a288 l_1_bit_register_0a47a288_64 (
    .Send(in_64), .Load(in_65), .D0(out_67), .CLK(CLK), .Q0(out_67));
  L_1_bit_register_0a47a288 l_1_bit_register_0a47a288_65 (
    .Send(in_2), .Load(in_3), .D0(out_68), .CLK(CLK), .Q0(out_68));
  L_1_bit_register_0a47a288 l_1_bit_register_0a47a288_66 (
    .Send(in_4), .Load(in_5), .D0(out_68), .CLK(CLK), .Q0(out_68));
  L_1_bit_register_0a47a288 l_1_bit_register_0a47a288_67 (
    .Send(in_6), .Load(in_7), .D0(out_68), .CLK(CLK), .Q0(out_68));
  L_1_bit_register_0a47a288 l_1_bit_register_0a47a288_68 (
    .Send(in_8), .Load(in_9), .D0(out_68), .CLK(CLK), .Q0(out_68));
  L_1_bit_register_0a47a288 l_1_bit_register_0a47a288_69 (
    .Send(in_10), .Load(in_11), .D0(out_68), .CLK(CLK), .Q0(out_68));
  L_1_bit_register_0a47a288 l_1_bit_register_0a47a288_70 (
    .Send(in_12), .Load(in_13), .D0(out_68), .CLK(CLK), .Q0(out_68));
  L_1_bit_register_0a47a288 l_1_bit_register_0a47a288_71 (
    .Send(in_14), .Load(in_15), .D0(out_68), .CLK(CLK), .Q0(out_68));
  L_1_bit_register_0a47a288 l_1_bit_register_0a47a288_72 (
    .Send(in_16), .Load(in_17), .D0(out_68), .CLK(CLK), .Q0(out_68));
  L_1_bit_register_0a47a288 l_1_bit_register_0a47a288_73 (
    .Send(in_18), .Load(in_19), .D0(out_68), .CLK(CLK), .Q0(out_68));
  L_1_bit_register_0a47a288 l_1_bit_register_0a47a288_74 (
    .Send(in_20), .Load(in_21), .D0(out_68), .CLK(CLK), .Q0(out_68));
  L_1_bit_register_0a47a288 l_1_bit_register_0a47a288_75 (
    .Send(in_22), .Load(in_23), .D0(out_68), .CLK(CLK), .Q0(out_68));
  L_1_bit_register_0a47a288 l_1_bit_register_0a47a288_76 (
    .Send(in_24), .Load(in_25), .D0(out_68), .CLK(CLK), .Q0(out_68));
  L_1_bit_register_0a47a288 l_1_bit_register_0a47a288_77 (
    .Send(in_26), .Load(in_27), .D0(out_68), .CLK(CLK), .Q0(out_68));
  L_1_bit_register_0a47a288 l_1_bit_register_0a47a288_78 (
    .Send(in_28), .Load(in_29), .D0(out_68), .CLK(CLK), .Q0(out_68));
  L_1_bit_register_0a47a288 l_1_bit_register_0a47a288_79 (
    .Send(in_30), .Load(in_31), .D0(out_68), .CLK(CLK), .Q0(out_68));
  L_1_bit_register_0a47a288 l_1_bit_register_0a47a288_80 (
    .Send(in_32), .Load(in_33), .D0(out_68), .CLK(CLK), .Q0(out_68));
  L_1_bit_register_0a47a288 l_1_bit_register_0a47a288_81 (
    .Send(in_34), .Load(in_35), .D0(out_68), .CLK(CLK), .Q0(out_68));
  L_1_bit_register_0a47a288 l_1_bit_register_0a47a288_82 (
    .Send(in_36), .Load(in_37), .D0(out_68), .CLK(CLK), .Q0(out_68));
  L_1_bit_register_0a47a288 l_1_bit_register_0a47a288_83 (
    .Send(in_38), .Load(in_39), .D0(out_68), .CLK(CLK), .Q0(out_68));
  L_1_bit_register_0a47a288 l_1_bit_register_0a47a288_84 (
    .Send(in_40), .Load(in_41), .D0(out_68), .CLK(CLK), .Q0(out_68));
  L_1_bit_register_0a47a288 l_1_bit_register_0a47a288_85 (
    .Send(in_42), .Load(in_43), .D0(out_68), .CLK(CLK), .Q0(out_68));
  L_1_bit_register_0a47a288 l_1_bit_register_0a47a288_86 (
    .Send(in_44), .Load(in_45), .D0(out_68), .CLK(CLK), .Q0(out_68));
  L_1_bit_register_0a47a288 l_1_bit_register_0a47a288_87 (
    .Send(in_46), .Load(in_47), .D0(out_68), .CLK(CLK), .Q0(out_68));
  L_1_bit_register_0a47a288 l_1_bit_register_0a47a288_88 (
    .Send(in_48), .Load(in_49), .D0(out_68), .CLK(CLK), .Q0(out_68));
  L_1_bit_register_0a47a288 l_1_bit_register_0a47a288_89 (
    .Send(in_50), .Load(in_51), .D0(out_68), .CLK(CLK), .Q0(out_68));
  L_1_bit_register_0a47a288 l_1_bit_register_0a47a288_90 (
    .Send(in_52), .Load(in_53), .D0(out_68), .CLK(CLK), .Q0(out_68));
  L_1_bit_register_0a47a288 l_1_bit_register_0a47a288_91 (
    .Send(in_54), .Load(in_55), .D0(out_68), .CLK(CLK), .Q0(out_68));
  L_1_bit_register_0a47a288 l_1_bit_register_0a47a288_92 (
    .Send(in_56), .Load(in_57), .D0(out_68), .CLK(CLK), .Q0(out_68));
  L_1_bit_register_0a47a288 l_1_bit_register_0a47a288_93 (
    .Send(in_58), .Load(in_59), .D0(out_68), .CLK(CLK), .Q0(out_68));
  L_1_bit_register_0a47a288 l_1_bit_register_0a47a288_94 (
    .Send(in_60), .Load(in_61), .D0(out_68), .CLK(CLK), .Q0(out_68));
  L_1_bit_register_0a47a288 l_1_bit_register_0a47a288_95 (
    .Send(in_62), .Load(in_63), .D0(out_68), .CLK(CLK), .Q0(out_68));
  L_1_bit_register_0a47a288 l_1_bit_register_0a47a288_96 (
    .Send(in_64), .Load(in_65), .D0(out_68), .CLK(CLK), .Q0(out_68));
  L_1_bit_register_0a47a288 l_1_bit_register_0a47a288_97 (
    .Send(in_2), .Load(in_3), .D0(out_69), .CLK(CLK), .Q0(out_69));
  L_1_bit_register_0a47a288 l_1_bit_register_0a47a288_98 (
    .Send(in_4), .Load(in_5), .D0(out_69), .CLK(CLK), .Q0(out_69));
  L_1_bit_register_0a47a288 l_1_bit_register_0a47a288_99 (
    .Send(in_6), .Load(in_7), .D0(out_69), .CLK(CLK), .Q0(out_69));
  L_1_bit_register_0a47a288 l_1_bit_register_0a47a288_100 (
    .Send(in_8), .Load(in_9), .D0(out_69), .CLK(CLK), .Q0(out_69));
  L_1_bit_register_0a47a288 l_1_bit_register_0a47a288_101 (
    .Send(in_10), .Load(in_11), .D0(out_69), .CLK(CLK), .Q0(out_69));
  L_1_bit_register_0a47a288 l_1_bit_register_0a47a288_102 (
    .Send(in_12), .Load(in_13), .D0(out_69), .CLK(CLK), .Q0(out_69));
  L_1_bit_register_0a47a288 l_1_bit_register_0a47a288_103 (
    .Send(in_14), .Load(in_15), .D0(out_69), .CLK(CLK), .Q0(out_69));
  L_1_bit_register_0a47a288 l_1_bit_register_0a47a288_104 (
    .Send(in_16), .Load(in_17), .D0(out_69), .CLK(CLK), .Q0(out_69));
  L_1_bit_register_0a47a288 l_1_bit_register_0a47a288_105 (
    .Send(in_18), .Load(in_19), .D0(out_69), .CLK(CLK), .Q0(out_69));
  L_1_bit_register_0a47a288 l_1_bit_register_0a47a288_106 (
    .Send(in_20), .Load(in_21), .D0(out_69), .CLK(CLK), .Q0(out_69));
  L_1_bit_register_0a47a288 l_1_bit_register_0a47a288_107 (
    .Send(in_22), .Load(in_23), .D0(out_69), .CLK(CLK), .Q0(out_69));
  L_1_bit_register_0a47a288 l_1_bit_register_0a47a288_108 (
    .Send(in_24), .Load(in_25), .D0(out_69), .CLK(CLK), .Q0(out_69));
  L_1_bit_register_0a47a288 l_1_bit_register_0a47a288_109 (
    .Send(in_26), .Load(in_27), .D0(out_69), .CLK(CLK), .Q0(out_69));
  L_1_bit_register_0a47a288 l_1_bit_register_0a47a288_110 (
    .Send(in_28), .Load(in_29), .D0(out_69), .CLK(CLK), .Q0(out_69));
  L_1_bit_register_0a47a288 l_1_bit_register_0a47a288_111 (
    .Send(in_30), .Load(in_31), .D0(out_69), .CLK(CLK), .Q0(out_69));
  L_1_bit_register_0a47a288 l_1_bit_register_0a47a288_112 (
    .Send(in_32), .Load(in_33), .D0(out_69), .CLK(CLK), .Q0(out_69));
  L_1_bit_register_0a47a288 l_1_bit_register_0a47a288_113 (
    .Send(in_34), .Load(in_35), .D0(out_69), .CLK(CLK), .Q0(out_69));
  L_1_bit_register_0a47a288 l_1_bit_register_0a47a288_114 (
    .Send(in_36), .Load(in_37), .D0(out_69), .CLK(CLK), .Q0(out_69));
  L_1_bit_register_0a47a288 l_1_bit_register_0a47a288_115 (
    .Send(in_38), .Load(in_39), .D0(out_69), .CLK(CLK), .Q0(out_69));
  L_1_bit_register_0a47a288 l_1_bit_register_0a47a288_116 (
    .Send(in_40), .Load(in_41), .D0(out_69), .CLK(CLK), .Q0(out_69));
  L_1_bit_register_0a47a288 l_1_bit_register_0a47a288_117 (
    .Send(in_42), .Load(in_43), .D0(out_69), .CLK(CLK), .Q0(out_69));
  L_1_bit_register_0a47a288 l_1_bit_register_0a47a288_118 (
    .Send(in_44), .Load(in_45), .D0(out_69), .CLK(CLK), .Q0(out_69));
  L_1_bit_register_0a47a288 l_1_bit_register_0a47a288_119 (
    .Send(in_46), .Load(in_47), .D0(out_69), .CLK(CLK), .Q0(out_69));
  L_1_bit_register_0a47a288 l_1_bit_register_0a47a288_120 (
    .Send(in_48), .Load(in_49), .D0(out_69), .CLK(CLK), .Q0(out_69));
  L_1_bit_register_0a47a288 l_1_bit_register_0a47a288_121 (
    .Send(in_50), .Load(in_51), .D0(out_69), .CLK(CLK), .Q0(out_69));
  L_1_bit_register_0a47a288 l_1_bit_register_0a47a288_122 (
    .Send(in_52), .Load(in_53), .D0(out_69), .CLK(CLK), .Q0(out_69));
  L_1_bit_register_0a47a288 l_1_bit_register_0a47a288_123 (
    .Send(in_54), .Load(in_55), .D0(out_69), .CLK(CLK), .Q0(out_69));
  L_1_bit_register_0a47a288 l_1_bit_register_0a47a288_124 (
    .Send(in_56), .Load(in_57), .D0(out_69), .CLK(CLK), .Q0(out_69));
  L_1_bit_register_0a47a288 l_1_bit_register_0a47a288_125 (
    .Send(in_58), .Load(in_59), .D0(out_69), .CLK(CLK), .Q0(out_69));
  L_1_bit_register_0a47a288 l_1_bit_register_0a47a288_126 (
    .Send(in_60), .Load(in_61), .D0(out_69), .CLK(CLK), .Q0(out_69));
  L_1_bit_register_0a47a288 l_1_bit_register_0a47a288_127 (
    .Send(in_62), .Load(in_63), .D0(out_69), .CLK(CLK), .Q0(out_69));
  L_1_bit_register_0a47a288 l_1_bit_register_0a47a288_128 (
    .Send(in_64), .Load(in_65), .D0(out_69), .CLK(CLK), .Q0(out_69));
  L_1_bit_register_0a47a288 l_1_bit_register_0a47a288_129 (
    .Send(in_2), .Load(in_3), .D0(out_70), .CLK(CLK), .Q0(out_70));
  L_1_bit_register_0a47a288 l_1_bit_register_0a47a288_130 (
    .Send(in_4), .Load(in_5), .D0(out_70), .CLK(CLK), .Q0(out_70));
  L_1_bit_register_0a47a288 l_1_bit_register_0a47a288_131 (
    .Send(in_6), .Load(in_7), .D0(out_70), .CLK(CLK), .Q0(out_70));
  L_1_bit_register_0a47a288 l_1_bit_register_0a47a288_132 (
    .Send(in_8), .Load(in_9), .D0(out_70), .CLK(CLK), .Q0(out_70));
  L_1_bit_register_0a47a288 l_1_bit_register_0a47a288_133 (
    .Send(in_10), .Load(in_11), .D0(out_70), .CLK(CLK), .Q0(out_70));
  L_1_bit_register_0a47a288 l_1_bit_register_0a47a288_134 (
    .Send(in_12), .Load(in_13), .D0(out_70), .CLK(CLK), .Q0(out_70));
  L_1_bit_register_0a47a288 l_1_bit_register_0a47a288_135 (
    .Send(in_14), .Load(in_15), .D0(out_70), .CLK(CLK), .Q0(out_70));
  L_1_bit_register_0a47a288 l_1_bit_register_0a47a288_136 (
    .Send(in_16), .Load(in_17), .D0(out_70), .CLK(CLK), .Q0(out_70));
  L_1_bit_register_0a47a288 l_1_bit_register_0a47a288_137 (
    .Send(in_18), .Load(in_19), .D0(out_70), .CLK(CLK), .Q0(out_70));
  L_1_bit_register_0a47a288 l_1_bit_register_0a47a288_138 (
    .Send(in_20), .Load(in_21), .D0(out_70), .CLK(CLK), .Q0(out_70));
  L_1_bit_register_0a47a288 l_1_bit_register_0a47a288_139 (
    .Send(in_22), .Load(in_23), .D0(out_70), .CLK(CLK), .Q0(out_70));
  L_1_bit_register_0a47a288 l_1_bit_register_0a47a288_140 (
    .Send(in_24), .Load(in_25), .D0(out_70), .CLK(CLK), .Q0(out_70));
  L_1_bit_register_0a47a288 l_1_bit_register_0a47a288_141 (
    .Send(in_26), .Load(in_27), .D0(out_70), .CLK(CLK), .Q0(out_70));
  L_1_bit_register_0a47a288 l_1_bit_register_0a47a288_142 (
    .Send(in_28), .Load(in_29), .D0(out_70), .CLK(CLK), .Q0(out_70));
  L_1_bit_register_0a47a288 l_1_bit_register_0a47a288_143 (
    .Send(in_30), .Load(in_31), .D0(out_70), .CLK(CLK), .Q0(out_70));
  L_1_bit_register_0a47a288 l_1_bit_register_0a47a288_144 (
    .Send(in_32), .Load(in_33), .D0(out_70), .CLK(CLK), .Q0(out_70));
  L_1_bit_register_0a47a288 l_1_bit_register_0a47a288_145 (
    .Send(in_34), .Load(in_35), .D0(out_70), .CLK(CLK), .Q0(out_70));
  L_1_bit_register_0a47a288 l_1_bit_register_0a47a288_146 (
    .Send(in_36), .Load(in_37), .D0(out_70), .CLK(CLK), .Q0(out_70));
  L_1_bit_register_0a47a288 l_1_bit_register_0a47a288_147 (
    .Send(in_38), .Load(in_39), .D0(out_70), .CLK(CLK), .Q0(out_70));
  L_1_bit_register_0a47a288 l_1_bit_register_0a47a288_148 (
    .Send(in_40), .Load(in_41), .D0(out_70), .CLK(CLK), .Q0(out_70));
  L_1_bit_register_0a47a288 l_1_bit_register_0a47a288_149 (
    .Send(in_42), .Load(in_43), .D0(out_70), .CLK(CLK), .Q0(out_70));
  L_1_bit_register_0a47a288 l_1_bit_register_0a47a288_150 (
    .Send(in_44), .Load(in_45), .D0(out_70), .CLK(CLK), .Q0(out_70));
  L_1_bit_register_0a47a288 l_1_bit_register_0a47a288_151 (
    .Send(in_46), .Load(in_47), .D0(out_70), .CLK(CLK), .Q0(out_70));
  L_1_bit_register_0a47a288 l_1_bit_register_0a47a288_152 (
    .Send(in_48), .Load(in_49), .D0(out_70), .CLK(CLK), .Q0(out_70));
  L_1_bit_register_0a47a288 l_1_bit_register_0a47a288_153 (
    .Send(in_50), .Load(in_51), .D0(out_70), .CLK(CLK), .Q0(out_70));
  L_1_bit_register_0a47a288 l_1_bit_register_0a47a288_154 (
    .Send(in_52), .Load(in_53), .D0(out_70), .CLK(CLK), .Q0(out_70));
  L_1_bit_register_0a47a288 l_1_bit_register_0a47a288_155 (
    .Send(in_54), .Load(in_55), .D0(out_70), .CLK(CLK), .Q0(out_70));
  L_1_bit_register_0a47a288 l_1_bit_register_0a47a288_156 (
    .Send(in_56), .Load(in_57), .D0(out_70), .CLK(CLK), .Q0(out_70));
  L_1_bit_register_0a47a288 l_1_bit_register_0a47a288_157 (
    .Send(in_58), .Load(in_59), .D0(out_70), .CLK(CLK), .Q0(out_70));
  L_1_bit_register_0a47a288 l_1_bit_register_0a47a288_158 (
    .Send(in_60), .Load(in_61), .D0(out_70), .CLK(CLK), .Q0(out_70));
  L_1_bit_register_0a47a288 l_1_bit_register_0a47a288_159 (
    .Send(in_62), .Load(in_63), .D0(out_70), .CLK(CLK), .Q0(out_70));
  L_1_bit_register_0a47a288 l_1_bit_register_0a47a288_160 (
    .Send(in_64), .Load(in_65), .D0(out_70), .CLK(CLK), .Q0(out_70));
  L_1_bit_register_0a47a288 l_1_bit_register_0a47a288_161 (
    .Send(in_2), .Load(in_3), .D0(out_71), .CLK(CLK), .Q0(out_71));
  L_1_bit_register_0a47a288 l_1_bit_register_0a47a288_162 (
    .Send(in_4), .Load(in_5), .D0(out_71), .CLK(CLK), .Q0(out_71));
  L_1_bit_register_0a47a288 l_1_bit_register_0a47a288_163 (
    .Send(in_6), .Load(in_7), .D0(out_71), .CLK(CLK), .Q0(out_71));
  L_1_bit_register_0a47a288 l_1_bit_register_0a47a288_164 (
    .Send(in_8), .Load(in_9), .D0(out_71), .CLK(CLK), .Q0(out_71));
  L_1_bit_register_0a47a288 l_1_bit_register_0a47a288_165 (
    .Send(in_10), .Load(in_11), .D0(out_71), .CLK(CLK), .Q0(out_71));
  L_1_bit_register_0a47a288 l_1_bit_register_0a47a288_166 (
    .Send(in_12), .Load(in_13), .D0(out_71), .CLK(CLK), .Q0(out_71));
  L_1_bit_register_0a47a288 l_1_bit_register_0a47a288_167 (
    .Send(in_14), .Load(in_15), .D0(out_71), .CLK(CLK), .Q0(out_71));
  L_1_bit_register_0a47a288 l_1_bit_register_0a47a288_168 (
    .Send(in_16), .Load(in_17), .D0(out_71), .CLK(CLK), .Q0(out_71));
  L_1_bit_register_0a47a288 l_1_bit_register_0a47a288_169 (
    .Send(in_18), .Load(in_19), .D0(out_71), .CLK(CLK), .Q0(out_71));
  L_1_bit_register_0a47a288 l_1_bit_register_0a47a288_170 (
    .Send(in_20), .Load(in_21), .D0(out_71), .CLK(CLK), .Q0(out_71));
  L_1_bit_register_0a47a288 l_1_bit_register_0a47a288_171 (
    .Send(in_22), .Load(in_23), .D0(out_71), .CLK(CLK), .Q0(out_71));
  L_1_bit_register_0a47a288 l_1_bit_register_0a47a288_172 (
    .Send(in_24), .Load(in_25), .D0(out_71), .CLK(CLK), .Q0(out_71));
  L_1_bit_register_0a47a288 l_1_bit_register_0a47a288_173 (
    .Send(in_26), .Load(in_27), .D0(out_71), .CLK(CLK), .Q0(out_71));
  L_1_bit_register_0a47a288 l_1_bit_register_0a47a288_174 (
    .Send(in_28), .Load(in_29), .D0(out_71), .CLK(CLK), .Q0(out_71));
  L_1_bit_register_0a47a288 l_1_bit_register_0a47a288_175 (
    .Send(in_30), .Load(in_31), .D0(out_71), .CLK(CLK), .Q0(out_71));
  L_1_bit_register_0a47a288 l_1_bit_register_0a47a288_176 (
    .Send(in_32), .Load(in_33), .D0(out_71), .CLK(CLK), .Q0(out_71));
  L_1_bit_register_0a47a288 l_1_bit_register_0a47a288_177 (
    .Send(in_34), .Load(in_35), .D0(out_71), .CLK(CLK), .Q0(out_71));
  L_1_bit_register_0a47a288 l_1_bit_register_0a47a288_178 (
    .Send(in_36), .Load(in_37), .D0(out_71), .CLK(CLK), .Q0(out_71));
  L_1_bit_register_0a47a288 l_1_bit_register_0a47a288_179 (
    .Send(in_38), .Load(in_39), .D0(out_71), .CLK(CLK), .Q0(out_71));
  L_1_bit_register_0a47a288 l_1_bit_register_0a47a288_180 (
    .Send(in_40), .Load(in_41), .D0(out_71), .CLK(CLK), .Q0(out_71));
  L_1_bit_register_0a47a288 l_1_bit_register_0a47a288_181 (
    .Send(in_42), .Load(in_43), .D0(out_71), .CLK(CLK), .Q0(out_71));
  L_1_bit_register_0a47a288 l_1_bit_register_0a47a288_182 (
    .Send(in_44), .Load(in_45), .D0(out_71), .CLK(CLK), .Q0(out_71));
  L_1_bit_register_0a47a288 l_1_bit_register_0a47a288_183 (
    .Send(in_46), .Load(in_47), .D0(out_71), .CLK(CLK), .Q0(out_71));
  L_1_bit_register_0a47a288 l_1_bit_register_0a47a288_184 (
    .Send(in_48), .Load(in_49), .D0(out_71), .CLK(CLK), .Q0(out_71));
  L_1_bit_register_0a47a288 l_1_bit_register_0a47a288_185 (
    .Send(in_50), .Load(in_51), .D0(out_71), .CLK(CLK), .Q0(out_71));
  L_1_bit_register_0a47a288 l_1_bit_register_0a47a288_186 (
    .Send(in_52), .Load(in_53), .D0(out_71), .CLK(CLK), .Q0(out_71));
  L_1_bit_register_0a47a288 l_1_bit_register_0a47a288_187 (
    .Send(in_54), .Load(in_55), .D0(out_71), .CLK(CLK), .Q0(out_71));
  L_1_bit_register_0a47a288 l_1_bit_register_0a47a288_188 (
    .Send(in_56), .Load(in_57), .D0(out_71), .CLK(CLK), .Q0(out_71));
  L_1_bit_register_0a47a288 l_1_bit_register_0a47a288_189 (
    .Send(in_58), .Load(in_59), .D0(out_71), .CLK(CLK), .Q0(out_71));
  L_1_bit_register_0a47a288 l_1_bit_register_0a47a288_190 (
    .Send(in_60), .Load(in_61), .D0(out_71), .CLK(CLK), .Q0(out_71));
  L_1_bit_register_0a47a288 l_1_bit_register_0a47a288_191 (
    .Send(in_62), .Load(in_63), .D0(out_71), .CLK(CLK), .Q0(out_71));
  L_1_bit_register_0a47a288 l_1_bit_register_0a47a288_192 (
    .Send(in_64), .Load(in_65), .D0(out_71), .CLK(CLK), .Q0(out_71));
  L_1_bit_register_0a47a288 l_1_bit_register_0a47a288_193 (
    .Send(in_2), .Load(in_3), .D0(out_72), .CLK(CLK), .Q0(out_72));
  L_1_bit_register_0a47a288 l_1_bit_register_0a47a288_194 (
    .Send(in_4), .Load(in_5), .D0(out_72), .CLK(CLK), .Q0(out_72));
  L_1_bit_register_0a47a288 l_1_bit_register_0a47a288_195 (
    .Send(in_6), .Load(in_7), .D0(out_72), .CLK(CLK), .Q0(out_72));
  L_1_bit_register_0a47a288 l_1_bit_register_0a47a288_196 (
    .Send(in_8), .Load(in_9), .D0(out_72), .CLK(CLK), .Q0(out_72));
  L_1_bit_register_0a47a288 l_1_bit_register_0a47a288_197 (
    .Send(in_10), .Load(in_11), .D0(out_72), .CLK(CLK), .Q0(out_72));
  L_1_bit_register_0a47a288 l_1_bit_register_0a47a288_198 (
    .Send(in_12), .Load(in_13), .D0(out_72), .CLK(CLK), .Q0(out_72));
  L_1_bit_register_0a47a288 l_1_bit_register_0a47a288_199 (
    .Send(in_14), .Load(in_15), .D0(out_72), .CLK(CLK), .Q0(out_72));
  L_1_bit_register_0a47a288 l_1_bit_register_0a47a288_200 (
    .Send(in_16), .Load(in_17), .D0(out_72), .CLK(CLK), .Q0(out_72));
  L_1_bit_register_0a47a288 l_1_bit_register_0a47a288_201 (
    .Send(in_18), .Load(in_19), .D0(out_72), .CLK(CLK), .Q0(out_72));
  L_1_bit_register_0a47a288 l_1_bit_register_0a47a288_202 (
    .Send(in_20), .Load(in_21), .D0(out_72), .CLK(CLK), .Q0(out_72));
  L_1_bit_register_0a47a288 l_1_bit_register_0a47a288_203 (
    .Send(in_22), .Load(in_23), .D0(out_72), .CLK(CLK), .Q0(out_72));
  L_1_bit_register_0a47a288 l_1_bit_register_0a47a288_204 (
    .Send(in_24), .Load(in_25), .D0(out_72), .CLK(CLK), .Q0(out_72));
  L_1_bit_register_0a47a288 l_1_bit_register_0a47a288_205 (
    .Send(in_26), .Load(in_27), .D0(out_72), .CLK(CLK), .Q0(out_72));
  L_1_bit_register_0a47a288 l_1_bit_register_0a47a288_206 (
    .Send(in_28), .Load(in_29), .D0(out_72), .CLK(CLK), .Q0(out_72));
  L_1_bit_register_0a47a288 l_1_bit_register_0a47a288_207 (
    .Send(in_30), .Load(in_31), .D0(out_72), .CLK(CLK), .Q0(out_72));
  L_1_bit_register_0a47a288 l_1_bit_register_0a47a288_208 (
    .Send(in_32), .Load(in_33), .D0(out_72), .CLK(CLK), .Q0(out_72));
  L_1_bit_register_0a47a288 l_1_bit_register_0a47a288_209 (
    .Send(in_34), .Load(in_35), .D0(out_72), .CLK(CLK), .Q0(out_72));
  L_1_bit_register_0a47a288 l_1_bit_register_0a47a288_210 (
    .Send(in_36), .Load(in_37), .D0(out_72), .CLK(CLK), .Q0(out_72));
  L_1_bit_register_0a47a288 l_1_bit_register_0a47a288_211 (
    .Send(in_38), .Load(in_39), .D0(out_72), .CLK(CLK), .Q0(out_72));
  L_1_bit_register_0a47a288 l_1_bit_register_0a47a288_212 (
    .Send(in_40), .Load(in_41), .D0(out_72), .CLK(CLK), .Q0(out_72));
  L_1_bit_register_0a47a288 l_1_bit_register_0a47a288_213 (
    .Send(in_42), .Load(in_43), .D0(out_72), .CLK(CLK), .Q0(out_72));
  L_1_bit_register_0a47a288 l_1_bit_register_0a47a288_214 (
    .Send(in_44), .Load(in_45), .D0(out_72), .CLK(CLK), .Q0(out_72));
  L_1_bit_register_0a47a288 l_1_bit_register_0a47a288_215 (
    .Send(in_46), .Load(in_47), .D0(out_72), .CLK(CLK), .Q0(out_72));
  L_1_bit_register_0a47a288 l_1_bit_register_0a47a288_216 (
    .Send(in_48), .Load(in_49), .D0(out_72), .CLK(CLK), .Q0(out_72));
  L_1_bit_register_0a47a288 l_1_bit_register_0a47a288_217 (
    .Send(in_50), .Load(in_51), .D0(out_72), .CLK(CLK), .Q0(out_72));
  L_1_bit_register_0a47a288 l_1_bit_register_0a47a288_218 (
    .Send(in_52), .Load(in_53), .D0(out_72), .CLK(CLK), .Q0(out_72));
  L_1_bit_register_0a47a288 l_1_bit_register_0a47a288_219 (
    .Send(in_54), .Load(in_55), .D0(out_72), .CLK(CLK), .Q0(out_72));
  L_1_bit_register_0a47a288 l_1_bit_register_0a47a288_220 (
    .Send(in_56), .Load(in_57), .D0(out_72), .CLK(CLK), .Q0(out_72));
  L_1_bit_register_0a47a288 l_1_bit_register_0a47a288_221 (
    .Send(in_58), .Load(in_59), .D0(out_72), .CLK(CLK), .Q0(out_72));
  L_1_bit_register_0a47a288 l_1_bit_register_0a47a288_222 (
    .Send(in_60), .Load(in_61), .D0(out_72), .CLK(CLK), .Q0(out_72));
  L_1_bit_register_0a47a288 l_1_bit_register_0a47a288_223 (
    .Send(in_62), .Load(in_63), .D0(out_72), .CLK(CLK), .Q0(out_72));
  L_1_bit_register_0a47a288 l_1_bit_register_0a47a288_224 (
    .Send(in_64), .Load(in_65), .D0(out_72), .CLK(CLK), .Q0(out_72));
  L_1_bit_register_0a47a288 l_1_bit_register_0a47a288_225 (
    .Send(in_2), .Load(in_3), .D0(out_73), .CLK(CLK), .Q0(out_73));
  L_1_bit_register_0a47a288 l_1_bit_register_0a47a288_226 (
    .Send(in_4), .Load(in_5), .D0(out_73), .CLK(CLK), .Q0(out_73));
  L_1_bit_register_0a47a288 l_1_bit_register_0a47a288_227 (
    .Send(in_6), .Load(in_7), .D0(out_73), .CLK(CLK), .Q0(out_73));
  L_1_bit_register_0a47a288 l_1_bit_register_0a47a288_228 (
    .Send(in_8), .Load(in_9), .D0(out_73), .CLK(CLK), .Q0(out_73));
  L_1_bit_register_0a47a288 l_1_bit_register_0a47a288_229 (
    .Send(in_10), .Load(in_11), .D0(l_1_bit_register_0a47a288_229_q0), .CLK(CLK),
    .Q0(l_1_bit_register_0a47a288_229_q0));
  L_1_bit_register_0a47a288 l_1_bit_register_0a47a288_230 (
    .Send(in_12), .Load(in_13), .D0(l_1_bit_register_0a47a288_229_q0), .CLK(CLK),
    .Q0(l_1_bit_register_0a47a288_229_q0));
  L_1_bit_register_0a47a288 l_1_bit_register_0a47a288_231 (
    .Send(in_14), .Load(in_15), .D0(l_1_bit_register_0a47a288_229_q0), .CLK(CLK),
    .Q0(l_1_bit_register_0a47a288_229_q0));
  L_1_bit_register_0a47a288 l_1_bit_register_0a47a288_232 (
    .Send(in_16), .Load(in_17), .D0(l_1_bit_register_0a47a288_229_q0), .CLK(CLK),
    .Q0(l_1_bit_register_0a47a288_229_q0));
  L_1_bit_register_0a47a288 l_1_bit_register_0a47a288_233 (
    .Send(in_18), .Load(in_19), .D0(l_1_bit_register_0a47a288_229_q0), .CLK(CLK),
    .Q0(l_1_bit_register_0a47a288_229_q0));
  L_1_bit_register_0a47a288 l_1_bit_register_0a47a288_234 (
    .Send(in_20), .Load(in_21), .D0(l_1_bit_register_0a47a288_229_q0), .CLK(CLK),
    .Q0(l_1_bit_register_0a47a288_229_q0));
  L_1_bit_register_0a47a288 l_1_bit_register_0a47a288_235 (
    .Send(in_22), .Load(in_23), .D0(l_1_bit_register_0a47a288_229_q0), .CLK(CLK),
    .Q0(l_1_bit_register_0a47a288_229_q0));
  L_1_bit_register_0a47a288 l_1_bit_register_0a47a288_236 (
    .Send(in_24), .Load(in_25), .D0(l_1_bit_register_0a47a288_229_q0), .CLK(CLK),
    .Q0(l_1_bit_register_0a47a288_229_q0));
  L_1_bit_register_0a47a288 l_1_bit_register_0a47a288_237 (
    .Send(in_26), .Load(in_27), .D0(l_1_bit_register_0a47a288_237_q0), .CLK(CLK),
    .Q0(l_1_bit_register_0a47a288_237_q0));
  L_1_bit_register_0a47a288 l_1_bit_register_0a47a288_238 (
    .Send(in_28), .Load(in_29), .D0(l_1_bit_register_0a47a288_237_q0), .CLK(CLK),
    .Q0(l_1_bit_register_0a47a288_237_q0));
  L_1_bit_register_0a47a288 l_1_bit_register_0a47a288_239 (
    .Send(in_30), .Load(in_31), .D0(l_1_bit_register_0a47a288_237_q0), .CLK(CLK),
    .Q0(l_1_bit_register_0a47a288_237_q0));
  L_1_bit_register_0a47a288 l_1_bit_register_0a47a288_240 (
    .Send(in_32), .Load(in_33), .D0(l_1_bit_register_0a47a288_237_q0), .CLK(CLK),
    .Q0(l_1_bit_register_0a47a288_237_q0));
  L_1_bit_register_0a47a288 l_1_bit_register_0a47a288_241 (
    .Send(in_34), .Load(in_35), .D0(l_1_bit_register_0a47a288_237_q0), .CLK(CLK),
    .Q0(l_1_bit_register_0a47a288_237_q0));
  L_1_bit_register_0a47a288 l_1_bit_register_0a47a288_242 (
    .Send(in_36), .Load(in_37), .D0(l_1_bit_register_0a47a288_237_q0), .CLK(CLK),
    .Q0(l_1_bit_register_0a47a288_237_q0));
  L_1_bit_register_0a47a288 l_1_bit_register_0a47a288_243 (
    .Send(in_38), .Load(in_39), .D0(l_1_bit_register_0a47a288_237_q0), .CLK(CLK),
    .Q0(l_1_bit_register_0a47a288_237_q0));
  L_1_bit_register_0a47a288 l_1_bit_register_0a47a288_244 (
    .Send(in_40), .Load(in_41), .D0(l_1_bit_register_0a47a288_237_q0), .CLK(CLK),
    .Q0(l_1_bit_register_0a47a288_237_q0));
  L_1_bit_register_0a47a288 l_1_bit_register_0a47a288_245 (
    .Send(in_42), .Load(in_43), .D0(l_1_bit_register_0a47a288_245_q0), .CLK(CLK),
    .Q0(l_1_bit_register_0a47a288_245_q0));
  L_1_bit_register_0a47a288 l_1_bit_register_0a47a288_246 (
    .Send(in_44), .Load(in_45), .D0(l_1_bit_register_0a47a288_245_q0), .CLK(CLK),
    .Q0(l_1_bit_register_0a47a288_245_q0));
  L_1_bit_register_0a47a288 l_1_bit_register_0a47a288_247 (
    .Send(in_46), .Load(in_47), .D0(l_1_bit_register_0a47a288_245_q0), .CLK(CLK),
    .Q0(l_1_bit_register_0a47a288_245_q0));
  L_1_bit_register_0a47a288 l_1_bit_register_0a47a288_248 (
    .Send(in_48), .Load(in_49), .D0(l_1_bit_register_0a47a288_245_q0), .CLK(CLK),
    .Q0(l_1_bit_register_0a47a288_245_q0));
  L_1_bit_register_0a47a288 l_1_bit_register_0a47a288_249 (
    .Send(in_50), .Load(in_51), .D0(l_1_bit_register_0a47a288_245_q0), .CLK(CLK),
    .Q0(l_1_bit_register_0a47a288_245_q0));
  L_1_bit_register_0a47a288 l_1_bit_register_0a47a288_250 (
    .Send(in_52), .Load(in_53), .D0(l_1_bit_register_0a47a288_245_q0), .CLK(CLK),
    .Q0(l_1_bit_register_0a47a288_245_q0));
  L_1_bit_register_0a47a288 l_1_bit_register_0a47a288_251 (
    .Send(in_54), .Load(in_55), .D0(l_1_bit_register_0a47a288_245_q0), .CLK(CLK),
    .Q0(l_1_bit_register_0a47a288_245_q0));
  L_1_bit_register_0a47a288 l_1_bit_register_0a47a288_252 (
    .Send(in_56), .Load(in_57), .D0(l_1_bit_register_0a47a288_245_q0), .CLK(CLK),
    .Q0(l_1_bit_register_0a47a288_245_q0));
  L_1_bit_register_0a47a288 l_1_bit_register_0a47a288_253 (
    .Send(in_58), .Load(in_59), .D0(l_1_bit_register_0a47a288_253_q0), .CLK(CLK),
    .Q0(l_1_bit_register_0a47a288_253_q0));
  L_1_bit_register_0a47a288 l_1_bit_register_0a47a288_254 (
    .Send(in_60), .Load(in_61), .D0(l_1_bit_register_0a47a288_253_q0), .CLK(CLK),
    .Q0(l_1_bit_register_0a47a288_253_q0));
  L_1_bit_register_0a47a288 l_1_bit_register_0a47a288_255 (
    .Send(in_62), .Load(in_63), .D0(l_1_bit_register_0a47a288_253_q0), .CLK(CLK),
    .Q0(l_1_bit_register_0a47a288_253_q0));
  L_1_bit_register_0a47a288 l_1_bit_register_0a47a288_256 (
    .Send(in_64), .Load(in_65), .D0(l_1_bit_register_0a47a288_253_q0), .CLK(CLK),
    .Q0(l_1_bit_register_0a47a288_253_q0));
endmodule

module MAR_4bit (
  input  CLK,
  input  Send,
  input  load,
  input  A0,
  input  A1,
  input  A2,
  input  A3,
  input  Select,
  input  CLR,
  input  B3,
  input  B2,
  input  B1,
  input  B0,
  output L0,
  output Y0,
  output L1,
  output Y1,
  output L2,
  output Y2,
  output L3,
  output Y3
);

  wire and_1_out, and_2_out, and_3_out, and_4_out, and_5_out, and_6_out, and_7_out, and_8_out, and_9_out,
       and_10_out, and_11_out, and_12_out, and_13_out, and_14_out, and_15_out, and_16_out, d_ff_1_q,
       d_ff_2_q, d_ff_3_q, d_ff_4_q, not_1_out, not_2_out, not_3_out, not_4_out, not_5_out, not_6_out,
       or_1_out, or_2_out, or_3_out, or_4_out;

  not not_1 (not_1_out, load);
  not not_2 (not_2_out, load);
  not not_3 (not_3_out, load);
  not not_4 (not_4_out, load);
  and and_1 (and_1_out, d_ff_1_q, not_1_out);
  and and_2 (and_2_out, load, A0);
  and and_3 (and_3_out, d_ff_2_q, not_2_out);
  and and_4 (and_4_out, load, A1);
  and and_5 (and_5_out, d_ff_3_q, not_3_out);
  and and_6 (and_6_out, load, A2);
  and and_7 (and_7_out, d_ff_4_q, not_4_out);
  and and_8 (and_8_out, load, A3);
  D_Flip_Flop d_ff_1 (.D(or_1_out), .clk(CLK), .Q(d_ff_1_q), .reset(CLR));  // open: Qn, preset
  or or_1 (or_1_out, and_1_out, and_2_out);
  D_Flip_Flop d_ff_2 (.D(or_2_out), .clk(CLK), .Q(d_ff_2_q), .reset(CLR));  // open: Qn, preset
  or or_2 (or_2_out, and_3_out, and_4_out);
  D_Flip_Flop d_ff_3 (.D(or_3_out), .clk(CLK), .Q(d_ff_3_q), .reset(CLR));  // open: Qn, preset
  or or_3 (or_3_out, and_5_out, and_6_out);
  D_Flip_Flop d_ff_4 (.D(or_4_out), .clk(CLK), .Q(d_ff_4_q), .reset(CLR));  // open: Qn, preset
  or or_4 (or_4_out, and_7_out, and_8_out);
  not not_5 (not_5_out, Select);
  not not_6 (not_6_out, not_5_out);
  and and_9 (and_9_out, d_ff_1_q, not_5_out);
  and and_10 (and_10_out, B3, not_6_out);
  and and_11 (and_11_out, d_ff_2_q, not_5_out);
  and and_12 (and_12_out, B2, not_6_out);
  and and_13 (and_13_out, d_ff_3_q, not_5_out);
  and and_14 (and_14_out, B1, not_6_out);
  and and_15 (and_15_out, d_ff_4_q, not_5_out);
  and and_16 (and_16_out, B0, not_6_out);
  or or_5 (L0, and_9_out, and_10_out);
  or or_6 (L1, and_11_out, and_12_out);
  or or_7 (L2, and_13_out, and_14_out);
  or or_8 (L3, and_15_out, and_16_out);
  assign Y0 = Send ? L0 : 1'bz;  // Controlled_Buffer controlled_buffer_1
  assign Y1 = Send ? L1 : 1'bz;  // Controlled_Buffer controlled_buffer_2
  assign Y2 = Send ? L2 : 1'bz;  // Controlled_Buffer controlled_buffer_3
  assign Y3 = Send ? L3 : 1'bz;  // Controlled_Buffer controlled_buffer_4
endmodule

module Mar_8bit (
  input  Send,
  input  CLK,
  input  load,
  input  A0,
  input  A1,
  input  A2,
  input  A3,
  input  A4,
  input  Send_Bus,
  input  A5,
  input  A6,
  input  B7,
  input  B6,
  input  B5,
  input  B4,
  input  B3,
  input  B2,
  input  B1,
  input  B0,
  input  A7,
  input  CLR,
  output Y0,
  output Y1,
  output Y2,
  output Y3,
  output Y4,
  output Y5,
  output B7_2,
  output B6_2,
  output B5_2,
  output B4_2,
  output B3_2,
  output B2_2,
  output B1_2,
  output Bus0,
  output Y6,
  output Y7
);

  wire and_1_out, and_2_out, and_3_out, and_4_out, and_5_out, and_6_out, and_7_out, and_8_out, and_9_out,
       and_10_out, and_11_out, and_12_out, and_13_out, and_14_out, and_15_out, and_16_out, d_ff_1_q,
       d_ff_2_q, d_ff_3_q, d_ff_4_q, d_ff_5_q, d_ff_6_q, d_ff_7_q, d_ff_8_q, not_1_out, not_2_out, not_3_out,
       not_4_out, not_5_out, not_6_out, not_7_out, not_8_out, or_1_out, or_2_out, or_3_out, or_4_out,
       or_5_out, or_6_out, or_7_out, or_8_out;

  not not_1 (not_1_out, load);
  not not_2 (not_2_out, load);
  not not_3 (not_3_out, load);
  not not_4 (not_4_out, load);
  not not_5 (not_5_out, load);
  not not_6 (not_6_out, load);
  not not_7 (not_7_out, load);
  not not_8 (not_8_out, load);
  and and_1 (and_1_out, d_ff_1_q, not_1_out);
  and and_2 (and_2_out, load, A0);
  and and_3 (and_3_out, d_ff_2_q, not_2_out);
  and and_4 (and_4_out, load, A1);
  and and_5 (and_5_out, d_ff_3_q, not_3_out);
  and and_6 (and_6_out, load, A2);
  and and_7 (and_7_out, d_ff_4_q, not_4_out);
  and and_8 (and_8_out, load, A3);
  and and_9 (and_9_out, d_ff_5_q, not_5_out);
  and and_10 (and_10_out, load, A4);
  and and_11 (and_11_out, d_ff_6_q, not_6_out);
  and and_12 (and_12_out, load, A5);
  and and_13 (and_13_out, d_ff_7_q, not_7_out);
  and and_14 (and_14_out, load, A6);
  and and_15 (and_15_out, d_ff_8_q, not_8_out);
  and and_16 (and_16_out, load, A7);
  D_Flip_Flop #(.trigger("falling")) d_ff_1 (.D(or_1_out), .clk(CLK), .Q(d_ff_1_q), .reset(CLR));  // open: Qn, preset
  or or_1 (or_1_out, and_1_out, and_2_out);
  D_Flip_Flop #(.trigger("falling")) d_ff_2 (.D(or_2_out), .clk(CLK), .Q(d_ff_2_q), .reset(CLR));  // open: Qn, preset
  or or_2 (or_2_out, and_3_out, and_4_out);
  D_Flip_Flop #(.trigger("falling")) d_ff_3 (.D(or_3_out), .clk(CLK), .Q(d_ff_3_q), .reset(CLR));  // open: Qn, preset
  or or_3 (or_3_out, and_5_out, and_6_out);
  D_Flip_Flop #(.trigger("falling")) d_ff_4 (.D(or_4_out), .clk(CLK), .Q(d_ff_4_q), .reset(CLR));  // open: Qn, preset
  or or_4 (or_4_out, and_7_out, and_8_out);
  D_Flip_Flop #(.trigger("falling")) d_ff_5 (.D(or_5_out), .clk(CLK), .Q(d_ff_5_q), .reset(CLR));  // open: Qn, preset
  or or_5 (or_5_out, and_9_out, and_10_out);
  D_Flip_Flop #(.trigger("falling")) d_ff_6 (.D(or_6_out), .clk(CLK), .Q(d_ff_6_q), .reset(CLR));  // open: Qn, preset
  or or_6 (or_6_out, and_11_out, and_12_out);
  D_Flip_Flop #(.trigger("falling")) d_ff_7 (.D(or_7_out), .clk(CLK), .Q(d_ff_7_q), .reset(CLR));  // open: Qn, preset
  or or_7 (or_7_out, and_13_out, and_14_out);
  D_Flip_Flop #(.trigger("falling")) d_ff_8 (.D(or_8_out), .clk(CLK), .Q(d_ff_8_q), .reset(CLR));  // open: Qn, preset
  or or_8 (or_8_out, and_15_out, and_16_out);
  assign Y0 = Send ? d_ff_1_q : 1'bz;  // Controlled_Buffer controlled_buffer_1
  assign Y1 = Send ? d_ff_2_q : 1'bz;  // Controlled_Buffer controlled_buffer_2
  assign Y2 = Send ? d_ff_3_q : 1'bz;  // Controlled_Buffer controlled_buffer_3
  assign Y3 = Send ? d_ff_4_q : 1'bz;  // Controlled_Buffer controlled_buffer_4
  assign Y4 = Send ? d_ff_5_q : 1'bz;  // Controlled_Buffer controlled_buffer_5
  assign Y5 = Send ? d_ff_6_q : 1'bz;  // Controlled_Buffer controlled_buffer_6
  assign Y6 = Send ? d_ff_7_q : 1'bz;  // Controlled_Buffer controlled_buffer_7
  assign Y7 = Send ? d_ff_8_q : 1'bz;  // Controlled_Buffer controlled_buffer_8
  assign B4_2 = Send_Bus ? B4 : 1'bz;  // Controlled_Buffer controlled_buffer_9
  assign B5_2 = Send_Bus ? B5 : 1'bz;  // Controlled_Buffer controlled_buffer_10
  assign B6_2 = Send_Bus ? B6 : 1'bz;  // Controlled_Buffer controlled_buffer_11
  assign B7_2 = Send_Bus ? B7 : 1'bz;  // Controlled_Buffer controlled_buffer_12
  assign Bus0 = Send_Bus ? B0 : 1'bz;  // Controlled_Buffer controlled_buffer_13
  assign B3_2 = Send_Bus ? B3 : 1'bz;  // Controlled_Buffer controlled_buffer_14
  assign B2_2 = Send_Bus ? B2 : 1'bz;  // Controlled_Buffer controlled_buffer_15
  assign B1_2 = Send_Bus ? B1 : 1'bz;  // Controlled_Buffer controlled_buffer_16
endmodule

module Program_counter (
  input  CLR,
  input  Load,
  input  send,
  input  Mode,
  input  Enable,
  input  CLK,
  input  [7:0] BusIn,
  output [7:0] BusOut,
  output L7,
  output L6,
  output L5,
  output L4,
  output L3,
  output L2,
  output L1,
  output L0
);

  Counter counter_1 (
    .clr(CLR), .load(Load), .up(Mode), .count(Enable), .clk(CLK), .D(BusIn),
    .Q({L7, L6, L5, L4, L3, L2, L1, L0}));  // open: carry
  assign BusOut = send ? {L7, L6, L5, L4, L3, L2, L1, L0} : 8'bz;  // Controlled_Buffer controlled_buffer_1
endmodule

module Hex_Decoder (
  input  D3,
  input  D2,
  input  D1,
  input  D0,
  output A,
  output B,
  output C,
  output D,
  output E,
  output F,
  output G
);

  wire and_1_out, and_2_out, and_3_out, and_4_out, and_5_out, and_6_out, and_7_out, and_8_out, and_9_out,
       and_10_out, and_11_out, and_12_out, and_13_out, and_14_out, and_15_out, and_16_out, and_17_out,
       and_18_out, and_19_out, and_20_out, and_21_out, and_22_out, and_23_out, and_24_out, and_25_out,
       and_26_out, and_27_out, and_28_out, and_29_out, and_30_out, and_31_out, and_32_out, and_33_out,
       not_1_out, not_2_out, not_3_out, not_4_out, or_1_out, or_2_out, or_3_out, or_4_out, or_5_out,
       or_6_out, or_7_out, or_8_out, or_9_out, or_10_out;

  not not_1 (not_1_out, D3);
  not not_2 (not_2_out, D2);
  not not_3 (not_3_out, D1);
  not not_4 (not_4_out, D0);
  and and_1 (and_1_out, not_1_out, not_2_out);
  and and_2 (and_2_out, not_3_out, D0);
  and and_3 (and_3_out, not_1_out, D2);
  and and_4 (and_4_out, not_3_out, not_4_out);
  and and_5 (and_5_out, D3, not_2_out);
  and and_6 (and_6_out, D1, D0);
  and and_7 (and_7_out, D3, D2);
  and and_8 (and_8_out, D2, D1);
  and and_9 (and_9_out, D3, D1);
  and and_10 (and_10_out, D1, not_4_out);
  and and_11 (and_11_out, not_1_out, D0);
  and and_12 (and_12_out, not_2_out, not_3_out);
  and and_13 (and_13_out, not_1_out, D1);
  and and_14 (and_14_out, and_1_out, and_2_out);
  and and_15 (and_15_out, and_3_out, and_4_out);
  and and_16 (and_16_out, and_5_out, and_6_out);
  and and_17 (and_17_out, and_7_out, and_2_out);
  and and_18 (and_18_out, and_3_out, and_2_out);
  and and_19 (and_19_out, and_8_out, not_4_out);
  and and_20 (and_20_out, and_9_out, D0);
  and and_21 (and_21_out, and_7_out, not_4_out);
  and and_22 (and_22_out, and_1_out, and_10_out);
  and and_23 (and_23_out, and_7_out, D1);
  and and_24 (and_24_out, and_8_out, D0);
  and and_25 (and_25_out, and_10_out, and_5_out);
  and and_26 (and_26_out, and_12_out, D0);
  and and_27 (and_27_out, and_3_out, not_3_out);
  and and_28 (and_28_out, and_1_out, D0);
  and and_29 (and_29_out, and_1_out, D1);
  and and_30 (and_30_out, and_13_out, D0);
  and and_31 (and_31_out, and_1_out, not_3_out);
  and and_32 (and_32_out, and_3_out, and_6_out);
  and and_33 (and_33_out, and_7_out, and_4_out);
  or or_1 (or_1_out, and_14_out, and_15_out);
  or or_2 (or_2_out, and_16_out, and_17_out);
  or or_3 (or_3_out, and_18_out, and_19_out);
  or or_4 (or_4_out, and_20_out, and_21_out);
  or or_5 (or_5_out, and_22_out, and_21_out);
  or or_6 (or_6_out, and_24_out, and_25_out);
  or or_7 (or_7_out, and_11_out, and_26_out);
  or or_8 (or_8_out, and_28_out, and_29_out);
  or or_9 (or_9_out, and_30_out, and_17_out);
  or or_10 (or_10_out, and_31_out, and_32_out);
  or or_11 (A, or_1_out, or_2_out);
  or or_12 (B, or_3_out, or_4_out);
  or or_13 (C, or_5_out, and_23_out);
  or or_14 (D, or_1_out, or_6_out);
  or or_15 (E, or_7_out, and_27_out);
  or or_16 (F, or_8_out, or_9_out);
  or or_17 (G, or_10_out, and_33_out);
endmodule

module ControlUnit (
  input  CLR,
  input  Enable,
  input  I0,
  input  I1,
  input  I2,
  input  I3,
  input  CLK,
  output Counter_2,
  output Counter_1,
  output Counter_0,
  output S2,
  output S1,
  output S0,
  output DEC_IN,
  output DEC,
  output INC,
  output SUB,
  output Jump,
  output Counter_OUT,
  output Counter_Enable,
  output OutputRegister_IN,
  output BRegister_IN,
  output ALU_REG_OUT,
  output ARegister_OUT,
  output ARegister_IN,
  output InstructionRegister_IN,
  output InstructionRegister_OUT,
  output RAM_OUT,
  output RAM_IN,
  output MAR_IN,
  output HLT
);

  wire decoder_1_out6, not_1_out, or_1_out;

  or or_1 (or_1_out, CLR, decoder_1_out6);
  not not_1 (not_1_out, CLK);
  Counter #(.width(3), .max('h7)) u_counter_1 (
    .clr(or_1_out), .up(Enable), .count(Enable), .clk(not_1_out), .Q({Counter_2, Counter_1, Counter_0}));  // open: load, D, carry
  Decoder #(.select(3), .enable("false")) decoder_1 (
    .out6(decoder_1_out6), .sel({Counter_2, Counter_1, Counter_0}));  // open: out0, out1, out2, out3, out4, out5, out7
  ROM #(.addrWidth(7), .dataWidth(21)) rom_1 (
    .addr({I3, I2, I1, I0, Counter_2, Counter_1, Counter_0}),
    .data({HLT, MAR_IN, RAM_IN, RAM_OUT, InstructionRegister_OUT, InstructionRegister_IN, ARegister_IN, ARegister_OUT, ALU_REG_OUT, BRegister_IN, OutputRegister_IN, Counter_Enable, Counter_OUT, Jump, SUB, INC, DEC, DEC_IN, S0, S1, S2}));

  // Notes on the sheet:
  //   Resets on the 6 since none of the instructions are longer than 6 steps ==> saving a clock cycle 
  //   contents of rom_1 (hex, n*v repeats v):
  //   80100 28200 6*0 80100 28200 90000 24000 4*0 80100 28200 90000 20800 5000 0 0 0 80100 28200 90000
  //   20800 5041 0 0 0 80100 28200 90000 42000 4*0 80100 28200 14000 5*0 80100 28200 10080 5*0 80100 28200
  //   90000 20800 5002 0 0 0 80100 28200 90000 5003 4*0 80100 28200 90000 5024 4*0 80100 28200 90000 501d
  //   4*0 80100 28200 90000 20800 5006 0 0 0 80100 28200 90000 20800 5007 0 0 0 80100 28200 2400 5*0 80100
  //   28200 100000
endmodule

module CPU (
);

  wire [6:0] undriven;

  L_8_register_1c04c8bc l_8_register_1c04c8bc_1 (
    .Q3_LED(undriven[6]), .Q2_LED(undriven[5]), .Q1_LED(undriven[4]), .Q0_LED(undriven[3]));  // open: Send, Load, D0, D1, D2, D3, D4, D5, D6, D7, Q0, Q1, Q2, Q3, Q4, Q5, Q6, Q7, Q7_LED, Q6_LED, Q5_LED, Q4_LED, L0, L1, L2, L3, L4, L5, L6, L7, CLK, CLR
  ROM #(.addrWidth(7), .dataWidth(16)) rom_1 (.addr(undriven));  // open: data
endmodule

module Instruction_Register (
  input  Send,
  input  Load,
  input  D0,
  input  CLK,
  input  D1,
  input  D2,
  input  D3,
  input  D4,
  input  D5,
  input  D6,
  input  D7,
  input  CLR,
  output Q7_LED,
  output Q6_LED,
  output Q5_LED,
  output Q4_LED,
  output Q3_LED,
  output Q2_LED,
  output out_19,
  output out_20,
  output out_21,
  output out_22,
  output out_23,
  output out_24,
  output out_25,
  output out_26,
  output out_27,
  output out_28,
  output Q0,
  output Q1,
  output Q2,
  output Q3,
  output Q4,
  output Q5,
  output Q6,
  output Q7
);

  wire and_1_out, and_2_out, and_3_out, and_4_out, and_5_out, and_6_out, and_7_out, and_8_out, and_9_out,
       and_10_out, and_11_out, and_12_out, and_13_out, and_14_out, and_15_out, and_16_out, not_1_out,
       not_2_out, not_3_out, not_4_out, not_5_out, not_6_out, not_7_out, not_8_out, or_1_out, or_2_out,
       or_3_out, or_4_out, or_5_out, or_6_out, or_7_out, or_8_out;

  not not_1 (not_1_out, Load);
  not not_2 (not_2_out, Load);
  not not_3 (not_3_out, Load);
  not not_4 (not_4_out, Load);
  not not_5 (not_5_out, Load);
  not not_6 (not_6_out, Load);
  not not_7 (not_7_out, Load);
  not not_8 (not_8_out, Load);
  and and_1 (and_1_out, out_20, not_1_out);
  and and_2 (and_2_out, Load, D0);
  and and_3 (and_3_out, out_19, not_2_out);
  and and_4 (and_4_out, Load, D1);
  and and_5 (and_5_out, Q2_LED, not_3_out);
  and and_6 (and_6_out, Load, D2);
  and and_7 (and_7_out, out_25, not_4_out);
  and and_8 (and_8_out, Load, D3);
  and and_9 (and_9_out, out_24, not_5_out);
  and and_10 (and_10_out, Load, D4);
  and and_11 (and_11_out, out_23, not_6_out);
  and and_12 (and_12_out, Load, D5);
  and and_13 (and_13_out, out_22, not_7_out);
  and and_14 (and_14_out, Load, D6);
  and and_15 (and_15_out, out_21, not_8_out);
  and and_16 (and_16_out, Load, D7);
  or or_1 (or_1_out, and_1_out, and_2_out);
  or or_2 (or_2_out, and_3_out, and_4_out);
  or or_3 (or_3_out, and_5_out, and_6_out);
  or or_4 (or_4_out, and_7_out, and_8_out);
  or or_5 (or_5_out, and_9_out, and_10_out);
  or or_6 (or_6_out, and_11_out, and_12_out);
  or or_7 (or_7_out, and_13_out, and_14_out);
  or or_8 (or_8_out, and_15_out, and_16_out);
  D_Flip_Flop #(.trigger("falling")) d_ff_1 (.D(or_1_out), .clk(CLK), .Q(out_20), .reset(CLR));  // open: Qn, preset
  D_Flip_Flop #(.trigger("falling")) d_ff_2 (.D(or_2_out), .clk(CLK), .Q(out_19), .reset(CLR));  // open: Qn, preset
  D_Flip_Flop #(.trigger("falling")) d_ff_3 (.D(or_3_out), .clk(CLK), .Q(Q2_LED), .reset(CLR));  // open: Qn, preset
  D_Flip_Flop #(.trigger("falling")) d_ff_4 (.D(or_4_out), .clk(CLK), .Q(out_25), .reset(CLR));  // open: Qn, preset
  D_Flip_Flop #(.trigger("falling")) d_ff_5 (.D(or_5_out), .clk(CLK), .Q(out_24), .reset(CLR));  // open: Qn, preset
  D_Flip_Flop #(.trigger("falling")) d_ff_6 (.D(or_6_out), .clk(CLK), .Q(out_23), .reset(CLR));  // open: Qn, preset
  D_Flip_Flop #(.trigger("falling")) d_ff_7 (.D(or_7_out), .clk(CLK), .Q(out_22), .reset(CLR));  // open: Qn, preset
  D_Flip_Flop #(.trigger("falling")) d_ff_8 (.D(or_8_out), .clk(CLK), .Q(out_21), .reset(CLR));  // open: Qn, preset
  assign Q0 = Send ? out_20 : 1'bz;  // Controlled_Buffer controlled_buffer_1
  assign Q1 = Send ? out_19 : 1'bz;  // Controlled_Buffer controlled_buffer_2
  assign Q2 = Send ? Q2_LED : 1'bz;  // Controlled_Buffer controlled_buffer_3
  assign Q3 = Send ? out_25 : 1'bz;  // Controlled_Buffer controlled_buffer_4

  assign out_27 = out_19;
  assign out_28 = out_20;
  assign Q3_LED = out_25;
  assign Q4 = out_24;
  assign Q4_LED = out_24;
  assign Q5 = out_23;
  assign Q5_LED = out_23;
  assign Q6 = out_22;
  assign Q6_LED = out_22;
  assign Q7 = out_21;
  assign Q7_LED = out_21;
endmodule
module comp_check (
  input  CLK,
  output CLKIN,
  output CLR,
  output [2:0] out_4
);

  Counter #(.width(3), .max('h7), .trigger("falling")) counter_1 (
    .up(1'b1), .count(1'b1), .clk(CLK), .Q(out_4));  // open: clr, load, D, carry
  Decoder #(.select(3), .enable("false")) decoder_1 (
    .out4(CLKIN), .out5(CLR), .sel(out_4));  // open: out0, out1, out2, out3, out6, out7
endmodule

module RAM_BUS (
  input  send,
  input  in_2,
  input  in_3,
  input  in_4,
  input  in_5,
  input  in_6,
  input  in_7,
  input  in_8,
  input  L1,
  input  in_10,
  input  in_11,
  input  in_12,
  input  in_13,
  input  in_14,
  input  in_15,
  input  in_16,
  input  S0,
  input  load,
  output out_19,
  output out_20,
  output out_21,
  output out_22,
  output out_23,
  output out_24,
  output out_25,
  output out_26,
  output out_27,
  output out_28,
  output out_29,
  output out_30,
  output out_31,
  output out_32,
  output out_33,
  output out_34
);

  assign out_19 = send ? in_10 : 1'bz;  // Controlled_Buffer controlled_buffer_1
  assign out_22 = send ? in_13 : 1'bz;  // Controlled_Buffer controlled_buffer_2
  assign out_21 = send ? in_12 : 1'bz;  // Controlled_Buffer controlled_buffer_3
  assign out_20 = send ? in_11 : 1'bz;  // Controlled_Buffer controlled_buffer_4
  assign out_23 = send ? in_14 : 1'bz;  // Controlled_Buffer controlled_buffer_5
  assign out_24 = send ? in_15 : 1'bz;  // Controlled_Buffer controlled_buffer_6
  assign out_25 = send ? in_16 : 1'bz;  // Controlled_Buffer controlled_buffer_7
  assign out_26 = send ? S0 : 1'bz;  // Controlled_Buffer controlled_buffer_8
  assign out_27 = load ? in_2 : 1'bz;  // Controlled_Buffer controlled_buffer_9
  assign out_28 = load ? in_3 : 1'bz;  // Controlled_Buffer controlled_buffer_10
  assign out_29 = load ? in_4 : 1'bz;  // Controlled_Buffer controlled_buffer_11
  assign out_30 = load ? in_5 : 1'bz;  // Controlled_Buffer controlled_buffer_12
  assign out_31 = load ? in_6 : 1'bz;  // Controlled_Buffer controlled_buffer_13
  assign out_32 = load ? in_7 : 1'bz;  // Controlled_Buffer controlled_buffer_14
  assign out_33 = load ? in_8 : 1'bz;  // Controlled_Buffer controlled_buffer_15
  assign out_34 = load ? L1 : 1'bz;  // Controlled_Buffer controlled_buffer_16
endmodule

module ControlUnitJMP (
  input  CLR,
  input  Enable,
  input  CLK,
  input  I0,
  input  I1,
  input  I2,
  input  I3,
  input  CF,
  output Counter_2,
  output Counter_1,
  output Counter_0,
  output S2,
  output S1,
  output S0,
  output DEC_IN,
  output DEC,
  output INC,
  output SUB,
  output Jump,
  output Counter_OUT,
  output Counter_Enable,
  output OutputRegister_IN,
  output BRegister_IN,
  output ALU_REG_OUT,
  output ARegister_OUT,
  output ARegister_IN,
  output InstructionRegister_IN,
  output InstructionRegister_OUT,
  output RAM_OUT,
  output RAM_IN,
  output MAR_IN,
  output HLT,
  output FRI,
  output ALUI
);

  wire decoder_1_out6, not_1_out, or_1_out;

  not not_1 (not_1_out, CLK);
  or or_1 (or_1_out, CLR, decoder_1_out6);
  Counter #(.width(3), .max('h7)) u_counter_1 (
    .clr(or_1_out), .up(Enable), .count(Enable), .clk(not_1_out), .Q({Counter_2, Counter_1, Counter_0}));  // open: load, D, carry
  Decoder #(.select(3), .enable("false")) decoder_1 (
    .out6(decoder_1_out6), .sel({Counter_2, Counter_1, Counter_0}));  // open: out0, out1, out2, out3, out4, out5, out7
  ROM #(.dataWidth(23)) rom_1 (
    .addr({CF, I3, I2, I1, I0, Counter_2, Counter_1, Counter_0}),
    .data({ALUI, FRI, HLT, MAR_IN, RAM_IN, RAM_OUT, InstructionRegister_OUT, InstructionRegister_IN, ARegister_IN, ARegister_OUT, ALU_REG_OUT, BRegister_IN, OutputRegister_IN, Counter_Enable, Counter_OUT, Jump, SUB, INC, DEC, DEC_IN, S0, S1, S2}));

  // Notes on the sheet:
  //   Resets on the 6 since none of the instructions are longer than 6 steps ==> saving a clock cycle 
  //   contents of rom_1 (hex, n*v repeats v):
  //   80100 28200 6*0 80100 28200 90000 24000 4*0 80100 28200 90000 20800 605000 0 0 0 80100 28200 90000
  //   20800 605041 0 0 0 80100 28200 90000 42000 4*0 80100 28200 14000 5*0 80100 28200 10080 5*0 80100
  //   28200 90000 20800 605002 0 0 0 80100 28200 90000 605003 4*0 80100 28200 90000 605024 4*0 80100 28200
  //   90000 60501d 4*0 80100 28200 90000 20800 605006 0 0 0 80100 28200 90000 20800 605007 0 0 0 80100
  //   28200 2400 5*0 80100 28200 100000 5*0 80100 28200 6*0 80100 28200 6*0 80100 28200 90000 24000 4*0
  //   80100 28200 90000 20800 605000 0 0 0 80100 28200 90000 20800 605041 0 0 0 80100 28200 90000 42000
  //   4*0 80100 28200 14000 5*0 80100 28200 10080 5*0 80100 28200 90000 20800 605002 0 0 0 80100 28200
  //   90000 605003 4*0 80100 28200 90000 605024 4*0 80100 28200 90000 60501d 4*0 80100 28200 90000 20800
  //   605006 0 0 0 80100 28200 90000 20800 605007 0 0 0 80100 28200 2400 5*0 80100 28200 100000 5*0 80100
  //   28200 10080
endmodule
